// Logisim project s-mips.circ as structural Verilog: 28 circuits, main circuit S-MIPS Board
module S_MIPS_Board (
  input  DESHABILITAR_DISPATCHER,
  output halt
);

  wire button_1_out, CLK, CS, d_ff_1_q, LCLR, LoadRAM, LoadRAMOn, LW, R_R_W, R_W, ram_dispatcher_1_finished,
       RCS, Reset_out, RST, TTY_EN;
  wire [2:0] KDB;
  wire [3:0] LMask, Mask, ram_1_read_time, ram_1_write_time, RMask;
  wire [6:0] KDB_DATA, TTY_DATA;
  wire [15:0] Addr, LAddr, RAddr;
  wire [31:0] I0, I1, I2, I3, LData, ram_1_data_out_0, ram_1_data_out_1, ram_1_data_out_2, ram_1_data_out_3,
       RI0, RI1, RI2, RI3;

  TTY #(.rows(25), .cols(80)) tty_1 (.data(TTY_DATA), .clk(CLK), .we(TTY_EN), .clr(RST));
  not not_1 (LoadRAMOn, ram_dispatcher_1_finished);
  RAM_Dispatcher ram_dispatcher_1 (
    .WriteTime(ram_1_write_time), .Clock(CLK), .Data(LData), .Address(LAddr), .Mask(LMask),
    .Finished(ram_dispatcher_1_finished), .Write(LW), .CLR(LCLR));
  Keyboard #(.buflen(64)) keyboard_1 (.clk(CLK), .re(KDB[0]), .avail(KDB[2]), .data(KDB_DATA));  // open: clr
  RAM ram_1 (
    .Address(RAddr), .Data_Out_0(ram_1_data_out_0), .Data_Out_1(ram_1_data_out_1),
    .Data_Out_2(ram_1_data_out_2), .Data_Out_3(ram_1_data_out_3), .Data_In_0(RI0), .Data_In_1(RI1),
    .Data_In_2(RI2), .Data_In_3(RI3), .Mask(RMask), .nRead_Write(R_R_W), .Chip_Select(RCS),
    .Read_Time(ram_1_read_time), .Reset(button_1_out), .Write_Time(ram_1_write_time));
  Button button_1 (.out(button_1_out));
  D_Flip_Flop d_ff_1 (.clk(CLK), .D(1'b1), .Q(d_ff_1_q), .reset(Reset_out));  // open: Qn, preset, en
  Button Reset (.out(Reset_out));
  S_MIPS s_mips_1 (
    .Kbd_Enable(KDB[0]), .Address(Addr), .Kbd_Clear(KDB[1]), .Kbd_Available(KDB[2]), .RAM_In_0(I0),
    .Kbd_ASCII_Data(KDB_DATA), .RAM_In_1(I1), .TTY_Enable(TTY_EN), .RAM_In_2(I2), .RAM_In_3(I3),
    .TTY_ASCII_Data(TTY_DATA), .Reset(RST), .RAM_Out_0(ram_1_data_out_0), .Clock(CLK),
    .RAM_Out_1(ram_1_data_out_1), .Stop(halt), .RAM_Out_2(ram_1_data_out_2), .RAM_Out_3(ram_1_data_out_3),
    .Mask(Mask), .Read_Time(ram_1_read_time), .Write_Time(ram_1_write_time), .nRead_Write(R_W),
    .Chip_Select(CS));
  D_Flip_Flop d_ff_2 (.clk(CLK), .D(d_ff_1_q), .Qn(LCLR), .reset(Reset_out));  // open: Q, preset, en
  or or_1 (RST, LCLR, LoadRAM);
  Clock clock_1 (.out(CLK));
  Multiplexer #(.width(32), .enable("false")) multiplexer_1 (.in0(I0), .in1(LData), .out(RI0), .sel(LoadRAM));
  Multiplexer #(.width(32), .enable("false")) multiplexer_2 (.in0(I1), .in1(LData), .out(RI1), .sel(LoadRAM));
  Multiplexer #(.width(32), .enable("false")) multiplexer_3 (.in0(I2), .in1(LData), .out(RI2), .sel(LoadRAM));
  Multiplexer #(.width(32), .enable("false")) multiplexer_4 (.in0(I3), .in1(LData), .out(RI3), .sel(LoadRAM));
  and and_1 (LoadRAM, ~DESHABILITAR_DISPATCHER, LoadRAMOn);  // AND_Gate
  Multiplexer #(.width(16), .enable("false")) multiplexer_5 (.in0(Addr), .in1(LAddr), .out(RAddr), .sel(LoadRAM));
  Multiplexer #(.width(4), .enable("false")) multiplexer_6 (.in0(Mask), .in1(LMask), .out(RMask), .sel(LoadRAM));
  Multiplexer #(.enable("false")) multiplexer_7 (.in0(CS), .in1(LW), .out(RCS), .sel(LoadRAM));
  Multiplexer #(.enable("false")) multiplexer_8 (.in0(R_W), .in1(LW), .out(R_R_W), .sel(LoadRAM));

  // Notes on the sheet:
  //   NO MODIFICAR
  //   Keyboard
endmodule

module RAM (
  input  [15:0] Address,
  input  [31:0] Data_In_0,
  input  [31:0] Data_In_1,
  input  [31:0] Data_In_2,
  input  [31:0] Data_In_3,
  input  [3:0] Mask,
  input  nRead_Write,
  input  Chip_Select,
  input  Reset,
  output [31:0] Data_Out_0,
  output [31:0] Data_Out_1,
  output [31:0] Data_Out_2,
  output [31:0] Data_Out_3,
  output [3:0] Read_Time,
  output [3:0] Write_Time
);

  wire and_2_out, and_3_out, and_4_out, and_5_out, and_6_out, and_7_out, and_8_out, and_9_out, Changed, CLK,
       comparator_2_eq, comparator_3_eq, comparator_4_eq, comparator_5_eq, comparator_6_eq, Count,
       demultiplexer_3_out0, Idle, Idle_q, Load, Load0, Load1, nand_1_out, or_1_out, or_2_out, or_3_out,
       or_4_out, or_5_out, or_6_out, or_7_out, or_8_out, or_9_out, or_10_out, Proc_q, Update_Mem, Zero_Time;
  wire [3:0] counter_1_q, multiplexer_1_out, subtractor_1_out;
  wire [31:0] register_1_q, register_2_q, register_3_q, register_4_q, register_5_q;

  // Probe on 4'b0011
  // Probe on 4'b0010
  Multiplexer #(.width(4), .enable("false")) multiplexer_1 (
    .in0(4'b0011), .in1(4'b0010), .out(multiplexer_1_out), .sel(nRead_Write));
  or or_1 (or_1_out, Idle, Update_Mem);
  or or_2 (or_2_out, ~Chip_Select, Reset);  // OR_Gate
  Subtractor #(.width(4)) subtractor_1 (.a(multiplexer_1_out), .b(4'b0010), .out(subtractor_1_out));  // open: bin, bout
  D_Flip_Flop u_Idle (.clk(CLK), .D(or_1_out), .Q(Idle_q), .preset(or_2_out));  // open: Qn, en, reset
  Demultiplexer #(.enable("false")) demultiplexer_1 (.out0(Idle), .out1(Load0), .in(Idle_q), .sel(Changed));
  // Probe on counter_1_q
  Counter #(.width(4), .max('hf)) counter_1 (
    .load(Load), .D(subtractor_1_out), .count(Count), .Q(counter_1_q), .clk(CLK), .clr(or_3_out));  // open: carry
  or or_3 (or_3_out, ~Chip_Select, Reset);  // OR_Gate
  Comparator #(.width(4), .mode("unsigned")) comparator_1 (
    .a(4'b0000), .b(counter_1_q), .eq(Zero_Time));  // open: gt, lt
  or or_4 (or_4_out, Count, Load0, Load1);
  Register #(.width(32)) register_1 (.D(Data_In_0), .en(Chip_Select), .Q(register_1_q), .clk(CLK), .clr(or_5_out));
  or or_5 (or_5_out, ~Chip_Select, Reset);  // OR_Gate
  Register #(.width(32)) register_2 (.D(Data_In_1), .en(Chip_Select), .Q(register_2_q), .clk(CLK), .clr(or_6_out));
  or or_6 (or_6_out, ~Chip_Select, Reset);  // OR_Gate
  Register #(.width(32)) register_3 (.D(Data_In_2), .en(Chip_Select), .Q(register_3_q), .clk(CLK), .clr(or_7_out));
  or or_7 (or_7_out, ~Chip_Select, Reset);  // OR_Gate
  Register #(.width(32)) register_4 (.D(Data_In_3), .en(Chip_Select), .Q(register_4_q), .clk(CLK), .clr(or_8_out));
  or or_8 (or_8_out, ~Chip_Select, Reset);  // OR_Gate
  Register #(.width(32)) register_5 (
    .D({{11{1'b1}}, nRead_Write, Mask, Address}), .en(Chip_Select), .Q(register_5_q), .clk(CLK),
    .clr(or_9_out));
  or or_9 (or_9_out, ~Chip_Select, Reset);  // OR_Gate
  D_Flip_Flop Proc (.clk(CLK), .D(or_4_out), .Q(Proc_q), .reset(or_10_out));  // open: Qn, preset, en
  or or_10 (or_10_out, ~Chip_Select, Reset);  // OR_Gate
  Demultiplexer #(.enable("false")) demultiplexer_2 (
    .out0(Count), .out1(Update_Mem), .in(demultiplexer_3_out0), .sel(Zero_Time));
  Demultiplexer #(.enable("false")) demultiplexer_3 (
    .out0(demultiplexer_3_out0), .out1(Load1), .in(Proc_q), .sel(Changed));
  Clock clock_1 (.out(CLK));
  Comparator #(.width(32)) comparator_2 (.a(register_1_q), .b(Data_In_0), .eq(comparator_2_eq));  // open: gt, lt
  Comparator #(.width(32)) comparator_3 (.a(register_2_q), .b(Data_In_1), .eq(comparator_3_eq));  // open: gt, lt
  Comparator #(.width(32)) comparator_4 (.a(register_3_q), .b(Data_In_2), .eq(comparator_4_eq));  // open: gt, lt
  Comparator #(.width(32)) comparator_5 (.a(register_4_q), .b(Data_In_3), .eq(comparator_5_eq));  // open: gt, lt
  Comparator #(.width(32)) comparator_6 (
    .a(register_5_q), .b({{11{1'b1}}, nRead_Write, Mask, Address}), .eq(comparator_6_eq));  // open: gt, lt
  nand nand_1 (nand_1_out, comparator_6_eq, comparator_2_eq, comparator_3_eq, comparator_4_eq, comparator_5_eq);
  and and_1 (Changed, nand_1_out, Chip_Select);
  or or_11 (Load, Count, Load1, Load0);
  and and_2 (and_2_out, Mask[0], Update_Mem, nRead_Write);
  and and_3 (and_3_out, Mask[1], Update_Mem, nRead_Write);
  and and_4 (and_4_out, Mask[2], Update_Mem, nRead_Write);
  and and_5 (and_5_out, Mask[3], Update_Mem, nRead_Write);
  RAM_part #(.addrWidth(16), .dataWidth(32), .bus("separate")) ram_1 (
    .addr(Address), .din(Data_In_0), .data(Data_Out_0), .str(and_2_out), .sel(Chip_Select), .clk(CLK),
    .ld(and_6_out), .clr(Reset));
  and and_6 (and_6_out, ~nRead_Write, Idle);  // AND_Gate
  RAM_part #(.addrWidth(16), .dataWidth(32), .bus("separate")) ram_2 (
    .addr(Address), .din(Data_In_1), .data(Data_Out_1), .str(and_3_out), .sel(Chip_Select), .clk(CLK),
    .ld(and_7_out), .clr(Reset));
  and and_7 (and_7_out, ~nRead_Write, Idle);  // AND_Gate
  RAM_part #(.addrWidth(16), .dataWidth(32), .bus("separate")) ram_3 (
    .addr(Address), .din(Data_In_2), .data(Data_Out_2), .str(and_4_out), .sel(Chip_Select), .clk(CLK),
    .ld(and_8_out), .clr(Reset));
  and and_8 (and_8_out, ~nRead_Write, Idle);  // AND_Gate
  RAM_part #(.addrWidth(16), .dataWidth(32), .bus("separate")) ram_4 (
    .addr(Address), .din(Data_In_3), .data(Data_Out_3), .str(and_5_out), .sel(Chip_Select), .clk(CLK),
    .ld(and_9_out), .clr(Reset));
  and and_9 (and_9_out, ~nRead_Write, Idle);  // AND_Gate

  assign Read_Time = 4'b0011;
  assign Write_Time = 4'b0010;

  // Other names for the same wires on the sheet: M0 = Mask[0]; M1 = Mask[1]; M2 = Mask[2]; M3 = Mask[3];
  //   RW = nRead_Write; CLR = Reset; CS = Chip_Select; Load2 = Count

  // Notes on the sheet:
  //   NO MODIFICAR
  //   excepto quizás los valores RT y WT
  //   BANK0
  //   BANK1
  //   BANK2
  //   BANK3
endmodule

module S_MIPS (
  input  Kbd_Available,
  input  [31:0] RAM_Out_0,
  input  [6:0] Kbd_ASCII_Data,
  input  [31:0] RAM_Out_1,
  input  [31:0] RAM_Out_2,
  input  Reset,
  input  Clock,
  input  [31:0] RAM_Out_3,
  input  [3:0] Read_Time,
  input  [3:0] Write_Time,
  output [15:0] Address,
  output Kbd_Enable,
  output Kbd_Clear,
  output TTY_Enable,
  output [6:0] TTY_ASCII_Data,
  output Stop,
  output [31:0] RAM_In_0,
  output [31:0] RAM_In_1,
  output [31:0] RAM_In_2,
  output [31:0] RAM_In_3,
  output [3:0] Mask,
  output nRead_Write,
  output Chip_Select
);

  wire and_1_out, Cached, cu_4_1_invalidate_cache_address, Deactivate_nR_W, Inst_valid, Load_Registers,
       Load_SP, M_I__valid, PC_load, pop_lw_ready, Read_from_memory, Write_to_memory;
  wire [1:0] RAM_bank_sel;
  wire [2:0] OP_Code;
  wire [31:0] Cache_Out_0, Cache_Out_1, Cache_Out_2, Cache_Out_3, little_endian_adjuster_1_output,
       Mem_data_0, Mem_data_1, Mem_data_2, Mem_data_3, RAM_input;

  Multiplexer #(.width(32), .enable("false")) multiplexer_1 (
    .in0(RAM_Out_0), .in1(Cache_Out_0), .out(Mem_data_0), .sel(Cached));
  Multiplexer #(.width(32), .enable("false")) multiplexer_2 (
    .in0(RAM_Out_1), .in1(Cache_Out_1), .out(Mem_data_1), .sel(Cached));
  Multiplexer #(.width(32), .enable("false")) multiplexer_3 (
    .in0(RAM_Out_2), .in1(Cache_Out_2), .out(Mem_data_2), .sel(Cached));
  Multiplexer #(.width(32), .enable("false")) multiplexer_4 (
    .in0(RAM_Out_3), .in1(Cache_Out_3), .out(Mem_data_3), .sel(Cached));
  and and_1 (and_1_out, nRead_Write, Chip_Select);
  Little_Endian_adjuster little_endian_adjuster_1 (.Input(RAM_input), .Output(little_endian_adjuster_1_output));
  Demultiplexer #(.select(2), .width(32)) demultiplexer_1 (
    .out0(RAM_In_0), .out2(RAM_In_2), .out3(RAM_In_3), .in(little_endian_adjuster_1_output),
    .sel(RAM_bank_sel), .en(and_1_out));  // open: out1
  CU_4 cu_4_1 (
    .clk(Clock), .Reset(Reset), .RT(Read_Time), .WT(Write_Time), .OP_Sel(OP_Code), .CS(Chip_Select),
    .Inst_ready(Inst_valid), .PC_load(PC_load), .M_I__valid(M_I__valid), .stop(Stop),
    .Load_Registers(Load_Registers), .Load_SP(Load_SP), .tty_enable(TTY_Enable), .kbd_enable(Kbd_Enable),
    .Deactivate_nR_W(Deactivate_nR_W), .Cached(Cached), .pop_lw_ready(pop_lw_ready),
    .Invalidate_cache_address(cu_4_1_invalidate_cache_address));
  and and_2 (nRead_Write, Write_to_memory, ~Deactivate_nR_W);  // AND_Gate
  Data_Path data_path_1 (
    .clk(Clock), .kbd_data(Kbd_ASCII_Data), .kbd_available(Kbd_Available), .tty_data(TTY_ASCII_Data),
    .M_I__valid(M_I__valid), .Address_forRAM(Address), .RAM_input(RAM_input), .reset(Reset),
    .PC_Load(PC_load), .instruction_valid(Inst_valid), .RAM_Out_0(Mem_data_0), .RAM_Out_1(Mem_data_1),
    .RAM_Out_2(Mem_data_2), .RAM_Out_3(Mem_data_3), .Load_SP(Load_SP), .RAM_bank_sel(RAM_bank_sel),
    .Mask(Mask), .OP_Code(OP_Code), .Read_from_memory(Read_from_memory), .Write_from_memory(Write_to_memory),
    .Load_Registers(Load_Registers), .Deactivate_nR_W(Deactivate_nR_W));  // open: RF_Output_0, RF_Output_1, RF_Out_from_H_L, Output_6, Output_5, Output_9, Output_2, Output_3, Output_4, Output_8, Output, Output_10, Output_11, Output_7
  Cache cache_1 (
    .clk(Clock), .Address(Address), .Contains_current_address(Cached), .RAM_Out_0_2(Cache_Out_0),
    .RAM_Out_1_2(Cache_Out_1), .RAM_Out_2_2(Cache_Out_2), .RAM_Out_3_2(Cache_Out_3), .CS(Chip_Select),
    .nR_W(nRead_Write), .reset(Reset), .RAM_Out_0(RAM_Out_0), .RAM_Out_1(RAM_Out_1), .RAM_Out_2(RAM_Out_2),
    .RAM_Out_3(RAM_Out_3), .Inst_ready(Inst_valid), .pop_lw_ready(pop_lw_ready),
    .Invalidate_cache_address(cu_4_1_invalidate_cache_address));  // open: Output, Output_2, Output_3, Output_4, Output_5, Output_6, Output_7, Output_8, Output_9

  assign Kbd_Clear = Reset;

  // Other names for the same wires on the sheet: CLK = Clock; CLR = Reset; CS = Chip_Select;
  //   KBD_AVAIL = Kbd_Available; KBD_DATA[6:0] = Kbd_ASCII_Data; nRW = nRead_Write; RAM_A[15:0] = Address;
  //   RAM_INPUT_0[31:0] = RAM_In_0; RAM_INPUT_1[31:0] = RAM_In_1; RAM_INPUT_2[31:0] = RAM_In_2;
  //   RAM_INPUT_3[31:0] = RAM_In_3; RAM_MASK[3:0] = Mask; RAM_OUTPUT_0[31:0] = RAM_Out_0;
  //   RAM_OUTPUT_1[31:0] = RAM_Out_1; RAM_OUTPUT_2[31:0] = RAM_Out_2; RAM_OUTPUT_3[31:0] = RAM_Out_3;
  //   TTY_DATA[6:0] = TTY_ASCII_Data

  // Notes on the sheet:
  //   DATA TO RAM
  //   DATA WRITE MASK
  //   RAM ADDRESS
  //   DATA FROM RAM
  //   RAM TIMING
  //   RAM CONTROL
  //   Aquí van DP con ALU y RF, CU,ID y BC con PC
  //   KEYBOARD
  //   TTY
  //   SEQUENCING
endmodule

module RAM_Dispatcher (
  input  [3:0] WriteTime,
  input  Clock,
  input  CLR,
  output [31:0] Data,
  output [15:0] Address,
  output [3:0] Mask,
  output Finished,
  output Write
);

  wire demultiplexer_2_out1, demultiplexer_3_out1, End, IDLE_q, IncAddr, Load, or_1_out, or_2_out, While_q,
       WriteEnd;
  wire [3:0] counter_1_q;
  wire [31:0] CurrentAddress_q;

  Counter #(.width(32), .max('hffffffff)) CurrentAddress (
    .count(IncAddr), .Q({CurrentAddress_q[31:18], Address, CurrentAddress_q[1:0]}), .clk(Clock), .clr(CLR));  // open: load, D, carry
  or or_1 (or_1_out, IncAddr, demultiplexer_3_out1, Finished);
  D_Flip_Flop IDLE (.clk(Clock), .D(or_1_out), .Q(IDLE_q), .preset(CLR));  // open: Qn, en, reset
  Demultiplexer #(.enable("false")) demultiplexer_1 (.out0(Load), .out1(Finished), .in(IDLE_q), .sel(End));
  D_Flip_Flop While (.clk(Clock), .D(or_2_out), .Q(While_q), .reset(CLR));  // open: Qn, preset, en
  or or_2 (or_2_out, Write, Load);
  RAM_part #(.addrWidth(18), .dataWidth(32)) ram_1 (
    .addr({Address, CurrentAddress_q[1:0]}), .data(Data), .clk(Clock));  // open: sel, ld, clr
  Demultiplexer #(.enable("false")) demultiplexer_2 (
    .out0(Write), .out1(demultiplexer_2_out1), .in(While_q), .sel(WriteEnd));
  Decoder_part #(.select(2)) decoder_1 (
    .out0(Mask[0]), .out1(Mask[1]), .out2(Mask[2]), .out3(Mask[3]), .sel(CurrentAddress_q[1:0]));  // open: en
  Demultiplexer #(.enable("false")) demultiplexer_3 (
    .out0(IncAddr), .out1(demultiplexer_3_out1), .in(demultiplexer_2_out1), .sel(End));
  Counter #(.width(4), .max('hf)) counter_1 (
    .load(Load), .D(WriteTime), .count(Write), .Q(counter_1_q), .clk(Clock));  // open: carry, clr
  Comparator #(.width(32)) comparator_1 (.a(Data), .b({32{1'b1}}), .eq(End));  // open: gt, lt
  Comparator #(.width(4)) comparator_2 (.a(4'b0000), .b(counter_1_q), .eq(WriteEnd));  // open: gt, lt

  // Other names for the same wires on the sheet: CLK = Clock; Count = Write; WT[3:0] = WriteTime
endmodule

module ALU (
  input  [31:0] Input_0,
  input  [31:0] Input_1,
  input  [3:0] OpCode,
  input  [1:0] High_Sel,
  input  Enable_H,
  output [31:0] Result_Low,
  output [31:0] High,
  output _1_bit_S_I0___I1,
  output S_I0___I1
);

  wire Borrow_Out, Carry, S_I0___I1_t_t, U_I0___I1_t, U_I0___I1_t_t, undriven, unsigned_comparer_1_i0___i1_3;
  wire [31:0] add, \and , div_High, div_Low, divu_High, divu_Low, mult_High, mult_Low, mulu_High, mulu_Low,
       \nor , \or , S_I0___I1_t, sub, U_I0___I1, \xor ;

  Comparator #(.width(32)) comparator_1 (
    .a(Input_0), .b(Input_1), .gt(S_I0___I1_t_t), .eq(S_I0___I1), .lt(_1_bit_S_I0___I1));
  assign S_I0___I1_t = {{31{1'b0}}, _1_bit_S_I0___I1};  // Bit_Extender bit_extender_1
  Adder #(.width(32)) adder_1 (.a(Input_0), .b(Input_1), .out(add), .cout(Carry));  // open: cin
  Subtractor #(.width(32)) subtractor_1 (.a(Input_0), .b(Input_1), .out(sub), .bout(Borrow_Out));  // open: bin
  Multiplier #(.width(32)) multiplier_1 (.a(Input_0), .b(Input_1), .out(mulu_Low), .cout(mulu_High));  // open: cin
  Divider #(.width(32)) divider_1 (.a(Input_0), .b(Input_1), .out(divu_Low), .rem(divu_High));  // open: upper
  Unsigned_Comparer unsigned_comparer_1 (
    .Input_0(Input_0), .Input_1(Input_1), .I0___I1(U_I0___I1_t_t), .I0___I1_2(U_I0___I1_t),
    .I0___I1_3(unsigned_comparer_1_i0___i1_3));
  S_mult s_mult_1 (.I0(Input_0), .I1(Input_1), .Low(mult_Low), .High(mult_High));
  S_div s_div_1 (.I0(Input_0), .I1(Input_1), .Low(div_Low), .High(div_High));
  assign U_I0___I1 = {{31{1'b0}}, unsigned_comparer_1_i0___i1_3};  // Bit_Extender bit_extender_2
  assign \and  = Input_0 & Input_1;  // AND_Gate and_1, 32 bits wide
  assign \or  = Input_0 | Input_1;  // OR_Gate or_1, 32 bits wide
  assign \xor  = Input_0 ^ Input_1;  // XOR_Gate xor_1, 32 bits wide
  assign \nor  = ~(Input_0 | Input_1);  // NOR_Gate nor_1, 32 bits wide
  Multiplexer #(.select(4), .width(32)) multiplexer_1 (
    .in0(add), .in1(sub), .in2(\and ), .in3(mult_Low), .in4(mulu_Low), .in5(div_Low), .in6(divu_Low),
    .in7(\or ), .in8(\nor ), .in9(\xor ), .in11(S_I0___I1_t), .in12(U_I0___I1), .out(Result_Low),
    .sel(OpCode), .en(undriven));  // open: in10, in13, in14, in15
  Multiplexer #(.select(2), .width(32)) multiplexer_2 (
    .in0(mult_High), .in1(mulu_High), .in2(div_High), .in3(divu_High), .out(High), .sel(High_Sel));  // open: en

  // Other names for the same wires on the sheet: _1bit_S_I0___I1 = _1_bit_S_I0___I1

  // Notes on the sheet:
  //   Inputs
  //   Signed comparer
  //   add
  //   sub
  //   mulu
  //   divu
  //   Arithmetic Operations
  //   Unsigned comparer
  //   mult
  //   div
  //   and
  //   or
  //   xor
  //   nor
  //   Logical Operations
  //   Outputs
endmodule

module Unsigned_Comparer (
  input  [31:0] Input_0,
  input  [31:0] Input_1,
  output I0___I1,
  output I0___I1_2,
  output I0___I1_3
);

  wire and_1_out, and_2_out, and_4_out, and_5_out, Cmp, Cmp_t, Cmp_t_t, XOR;

  Comparator #(.width(32)) comparator_1 (
    .a({1'b0, Input_0[30:0]}), .b({1'b0, Input_1[30:0]}), .gt(Cmp_t_t), .eq(Cmp_t), .lt(Cmp));
  xor xor_1 (XOR, Input_0[31], Input_1[31]);
  and and_1 (and_1_out, XOR, Input_0[31]);
  and and_2 (and_2_out, ~XOR, Cmp_t_t);  // AND_Gate
  and and_3 (I0___I1_2, ~XOR, Cmp_t);  // AND_Gate
  and and_4 (and_4_out, XOR, Input_1[31]);
  or or_1 (I0___I1, and_1_out, and_2_out);
  or or_2 (I0___I1_3, and_4_out, and_5_out);
  and and_5 (and_5_out, ~XOR, Cmp);  // AND_Gate

  // Other names for the same wires on the sheet: I0without1[30:0] = Input_0[30:0]; MSB_I0 = Input_0[31];
  //   I1without1[30:0] = Input_1[30:0]; MSB_I1 = Input_1[31]

  // Notes on the sheet:
  //   Outputs
endmodule

module S_mult (
  input  [31:0] I0,
  input  [31:0] I1,
  output [31:0] Low,
  output [31:0] High
);

  wire adder_1_cout, XOR;
  wire [31:0] adder_1_out, adder_2_out, bit_extender_1_out, multiplexer_1_out, multiplexer_2_out,
       multiplier_1_cout, multiplier_1_out, negator_1_out, negator_2_out, not_1_out, not_2_out;

  xor xor_1 (XOR, I0[31], I1[31]);
  Multiplexer #(.width(32)) multiplexer_1 (
    .in0(I0), .in1(negator_1_out), .out(multiplexer_1_out), .sel(I0[31]));  // open: en
  Negator #(.width(32)) negator_1 (.in(I0), .out(negator_1_out));
  Multiplexer #(.width(32)) multiplexer_2 (
    .in0(I1), .in1(negator_2_out), .out(multiplexer_2_out), .sel(I1[31]));  // open: en
  Negator #(.width(32)) negator_2 (.in(I1), .out(negator_2_out));
  Multiplier #(.width(32)) multiplier_1 (
    .a(multiplexer_1_out), .b(multiplexer_2_out), .out(multiplier_1_out), .cout(multiplier_1_cout));  // open: cin
  assign not_1_out = ~multiplier_1_out;  // NOT_Gate not_1, 32 bits wide
  Adder #(.width(32)) adder_1 (.a(not_1_out), .b(32'h1), .out(adder_1_out), .cout(adder_1_cout));  // open: cin
  assign not_2_out = ~multiplier_1_cout;  // NOT_Gate not_2, 32 bits wide
  Adder #(.width(32)) adder_2 (.a(not_2_out), .b(bit_extender_1_out), .out(adder_2_out));  // open: cin, cout
  assign bit_extender_1_out = {{31{1'b0}}, adder_1_cout};  // Bit_Extender bit_extender_1
  Multiplexer #(.width(32)) multiplexer_3 (
    .in0(multiplier_1_out), .in1(adder_1_out), .out(Low), .sel(XOR));  // open: en
  Multiplexer #(.width(32)) multiplexer_4 (
    .in0(multiplier_1_cout), .in1(adder_2_out), .out(High), .sel(XOR));  // open: en

  // Other names for the same wires on the sheet: MSB_I0 = I0[31]; MSB_I1 = I1[31]
endmodule

module S_div (
  input  [31:0] I0,
  input  [31:0] I1,
  output [31:0] Low,
  output [31:0] High
);

  wire adder_1_cout, XOR;
  wire [31:0] adder_1_out, adder_2_out, bit_extender_1_out, divider_1_out, divider_1_rem, multiplexer_1_out,
       multiplexer_2_out, negator_1_out, negator_2_out, not_1_out, not_2_out;

  xor xor_1 (XOR, I0[31], I1[31]);
  Multiplexer #(.width(32)) multiplexer_1 (
    .in0(I0), .in1(negator_1_out), .out(multiplexer_1_out), .sel(I0[31]));  // open: en
  Negator #(.width(32)) negator_1 (.in(I0), .out(negator_1_out));
  Multiplexer #(.width(32)) multiplexer_2 (
    .in0(I1), .in1(negator_2_out), .out(multiplexer_2_out), .sel(I1[31]));  // open: en
  Negator #(.width(32)) negator_2 (.in(I1), .out(negator_2_out));
  Divider #(.width(32)) divider_1 (
    .a(multiplexer_1_out), .b(multiplexer_2_out), .out(divider_1_out), .rem(divider_1_rem));  // open: upper
  assign not_1_out = ~divider_1_out;  // NOT_Gate not_1, 32 bits wide
  Adder #(.width(32)) adder_1 (.a(not_1_out), .b(32'h1), .out(adder_1_out), .cout(adder_1_cout));  // open: cin
  assign not_2_out = ~divider_1_rem;  // NOT_Gate not_2, 32 bits wide
  Adder #(.width(32)) adder_2 (.a(not_2_out), .b(bit_extender_1_out), .out(adder_2_out));  // open: cin, cout
  assign bit_extender_1_out = {{31{1'b0}}, adder_1_cout};  // Bit_Extender bit_extender_1
  Multiplexer #(.width(32)) multiplexer_3 (.in0(divider_1_out), .in1(adder_1_out), .out(Low), .sel(XOR));  // open: en
  Multiplexer #(.width(32)) multiplexer_4 (.in0(divider_1_rem), .in1(adder_2_out), .out(High), .sel(XOR));  // open: en

  // Other names for the same wires on the sheet: MSB_I0 = I0[31]; MSB_I1 = I1[31]
endmodule

module Register_File (
  input  [4:0] Output0_Sel,
  input  [4:0] Output1_Sel,
  input  [4:0] Enable_Sel,
  input  Clock,
  input  [31:0] in_5,
  input  Load_Registers,
  input  Enable_H_L,
  input  H_L_Selector,
  input  [31:0] High_SP_Input,
  input  reset,
  input  pop,
  input  M_I__valid,
  input  push,
  input  Load_SP,
  output [31:0] Output_0,
  output [31:0] H_L,
  output [31:0] Output_1
);

  wire and_2_out, and_3_out, Enable_R1, Enable_R2, Enable_R3, Enable_R4, Enable_R5, Enable_R6, Enable_R7,
       Enable_R8, Enable_R9, Enable_R10, Enable_R11, Enable_R12, Enable_R13, Enable_R14, Enable_R15,
       Enable_R16, Enable_R17, Enable_R18, Enable_R19, Enable_R20, Enable_R21, Enable_R22, Enable_R23,
       Enable_R24, Enable_R25, Enable_R26, Enable_R27, Enable_R28, Enable_R29, Enable_R30, Enable_R31,
       Enable_SP;
  wire [4:0] and_1_out, multiplexer_3_out, or_2_out;
  wire [4:4] or_3_out;
  wire [31:0] High_Out, Input_for_SP, Low_Out, R0, R1, R2, R3, R4, R5, R6, R7, R8, R9, R10, R11, R12, R13,
       R14, R15, R16, R17, R18, R19, R20, R21, R22, R23, R24, R25, R26, R27, R28, R29, R30, R31;

  Demultiplexer #(.select(5)) demultiplexer_1 (
    .out1(Enable_R1), .out2(Enable_R2), .out3(Enable_R3), .out4(Enable_R4), .out5(Enable_R5),
    .out6(Enable_R6), .out7(Enable_R7), .out8(Enable_R8), .out9(Enable_R9), .out10(Enable_R10),
    .out11(Enable_R11), .out12(Enable_R12), .out13(Enable_R13), .out14(Enable_R14), .out15(Enable_R15),
    .out16(Enable_R16), .out17(Enable_R17), .out18(Enable_R18), .out19(Enable_R19), .out20(Enable_R20),
    .out21(Enable_R21), .out22(Enable_R22), .out23(Enable_R23), .out24(Enable_R24), .out25(Enable_R25),
    .out26(Enable_R26), .out27(Enable_R27), .out28(Enable_R28), .out29(Enable_R29), .out30(Enable_R30),
    .out31(Enable_R31), .in(1'b1), .sel(and_1_out));  // open: out0, en
  assign and_1_out = {5{Load_Registers}} & Enable_Sel;  // AND_Gate and_1, 5 bits wide
  Register #(.width(32)) u_R0 (.Q(R0), .clk(Clock), .clr(reset));  // open: D, en
  Register #(.width(32)) u_R4 (.D(in_5), .en(Enable_R4), .Q(R4), .clk(Clock), .clr(reset));
  Register #(.width(32)) u_R8 (.D(in_5), .en(Enable_R8), .Q(R8), .clk(Clock), .clr(reset));
  Register #(.width(32)) u_R12 (.D(in_5), .en(Enable_R12), .Q(R12), .clk(Clock), .clr(reset));
  Register #(.width(32)) u_R16 (.D(in_5), .en(Enable_R16), .Q(R16), .clk(Clock), .clr(reset));
  Register #(.width(32)) u_R20 (.D(in_5), .en(Enable_R20), .Q(R20), .clk(Clock), .clr(reset));
  Register #(.width(32)) u_R24 (.D(in_5), .en(Enable_R24), .Q(R24), .clk(Clock), .clr(reset));
  Register #(.width(32)) u_R28 (.D(in_5), .en(Enable_R28), .Q(R28), .clk(Clock), .clr(reset));
  Register #(.width(32)) High (.D(High_SP_Input), .en(Enable_H_L), .Q(High_Out), .clk(Clock), .clr(reset));
  Register #(.width(32)) u_R1 (.D(in_5), .en(Enable_R1), .Q(R1), .clk(Clock), .clr(reset));
  Register #(.width(32)) u_R5 (.D(in_5), .en(Enable_R5), .Q(R5), .clk(Clock), .clr(reset));
  Register #(.width(32)) u_R9 (.D(in_5), .en(Enable_R9), .Q(R9), .clk(Clock), .clr(reset));
  Register #(.width(32)) u_R13 (.D(in_5), .en(Enable_R13), .Q(R13), .clk(Clock), .clr(reset));
  Register #(.width(32)) u_R17 (.D(in_5), .en(Enable_R17), .Q(R17), .clk(Clock), .clr(reset));
  Register #(.width(32)) u_R21 (.D(in_5), .en(Enable_R21), .Q(R21), .clk(Clock), .clr(reset));
  Register #(.width(32)) u_R25 (.D(in_5), .en(Enable_R25), .Q(R25), .clk(Clock), .clr(reset));
  Register #(.width(32)) u_R29 (.D(in_5), .en(Enable_R29), .Q(R29), .clk(Clock), .clr(reset));
  Multiplexer #(.width(32)) multiplexer_1 (.in0(in_5), .in1(High_SP_Input), .out(Input_for_SP), .sel(pop));  // open: en
  Register #(.width(32)) Low (.D(in_5), .en(Enable_H_L), .Q(Low_Out), .clk(Clock), .clr(reset));
  and and_2 (and_2_out, M_I__valid, pop);
  Register #(.width(32)) u_R2 (.D(in_5), .en(Enable_R2), .Q(R2), .clk(Clock), .clr(reset));
  Register #(.width(32)) u_R6 (.D(in_5), .en(Enable_R6), .Q(R6), .clk(Clock), .clr(reset));
  Register #(.width(32)) u_R10 (.D(in_5), .en(Enable_R10), .Q(R10), .clk(Clock), .clr(reset));
  Register #(.width(32)) u_R14 (.D(in_5), .en(Enable_R14), .Q(R14), .clk(Clock), .clr(reset));
  Register #(.width(32)) u_R18 (.D(in_5), .en(Enable_R18), .Q(R18), .clk(Clock), .clr(reset));
  Register #(.width(32)) u_R22 (.D(in_5), .en(Enable_R22), .Q(R22), .clk(Clock), .clr(reset));
  Register #(.width(32)) u_R26 (.D(in_5), .en(Enable_R26), .Q(R26), .clk(Clock), .clr(reset));
  Register #(.width(32)) u_R30 (.D(in_5), .en(Enable_R30), .Q(R30), .clk(Clock), .clr(reset));
  or or_1 (Enable_SP, Enable_R31, and_2_out, and_3_out);
  and and_3 (and_3_out, Load_SP, push);
  Register #(.width(32)) u_R3 (.D(in_5), .en(Enable_R3), .Q(R3), .clk(Clock), .clr(reset));
  Register #(.width(32)) u_R7 (.D(in_5), .en(Enable_R7), .Q(R7), .clk(Clock), .clr(reset));
  Register #(.width(32)) u_R11 (.D(in_5), .en(Enable_R11), .Q(R11), .clk(Clock), .clr(reset));
  Register #(.width(32)) u_R15 (.D(in_5), .en(Enable_R15), .Q(R15), .clk(Clock), .clr(reset));
  Register #(.width(32)) u_R19 (.D(in_5), .en(Enable_R19), .Q(R19), .clk(Clock), .clr(reset));
  Register #(.width(32)) u_R23 (.D(in_5), .en(Enable_R23), .Q(R23), .clk(Clock), .clr(reset));
  Register #(.width(32)) u_R27 (.D(in_5), .en(Enable_R27), .Q(R27), .clk(Clock), .clr(reset));
  Register #(.width(32)) u_R31 (.D(Input_for_SP), .en(Enable_SP), .Q(R31), .clk(Clock), .clr(reset));
  assign or_2_out = Output0_Sel | {5{or_3_out[4]}};  // OR_Gate or_2, 5 bits wide
  Multiplexer #(.width(32), .enable("false")) multiplexer_2 (
    .in0(Low_Out), .in1(High_Out), .out(H_L), .sel(H_L_Selector));
  Multiplexer #(.width(5)) multiplexer_3 (
    .in0(Output1_Sel), .in1(Output0_Sel), .out(multiplexer_3_out), .sel(push));  // open: en
  Multiplexer #(.select(5), .width(32)) multiplexer_4 (
    .in0(R0), .in1(R1), .in2(R2), .in3(R3), .in4(R4), .in5(R5), .in6(R6), .in7(R7), .in8(R8), .in9(R9),
    .in10(R10), .in11(R11), .in12(R12), .in13(R13), .in14(R14), .in15(R15), .in16(R16), .in17(R17),
    .in18(R18), .in19(R19), .in20(R20), .in21(R21), .in22(R22), .in23(R23), .in24(R24), .in25(R25),
    .in26(R26), .in27(R27), .in28(R28), .in29(R29), .in30(R30), .in31(R31), .out(Output_0), .sel(or_2_out));  // open: en
  or or_3 (or_3_out[4], pop, push);
  Multiplexer #(.select(5), .width(32)) multiplexer_5 (
    .in0(R0), .in1(R1), .in2(R2), .in3(R3), .in4(R4), .in5(R5), .in6(R6), .in7(R7), .in8(R8), .in9(R9),
    .in10(R10), .in11(R11), .in12(R12), .in13(R13), .in14(R14), .in15(R15), .in16(R16), .in17(R17),
    .in18(R18), .in19(R19), .in20(R20), .in21(R21), .in22(R22), .in23(R23), .in24(R24), .in25(R25),
    .in26(R26), .in27(R27), .in28(R28), .in29(R29), .in30(R30), .in31(R31), .out(Output_1),
    .sel(multiplexer_3_out));  // open: en

  // Other names for the same wires on the sheet: LR = Load_Registers; clk = Clock; H_L_Sel = H_L_Selector;
  //   High_In[31:0] = High_SP_Input; Input[31:0] = in_5

  // Notes on the sheet:
  //   Output
endmodule

module Instruction_Decoder (
  input  [31:0] Data_From_RAM,
  input  Inst_valid,
  input  clk,
  input  [31:0] Rs_data,
  input  [31:0] Rt_data,
  input  [31:0] ALU_Result_L,
  input  [31:0] ALU_High_value,
  input  [31:0] RF_Out_from_H_L,
  input  [31:0] PC_value,
  input  [6:0] kbd_data,
  input  kbd_available,
  input  [31:0] M_I__result,
  input  M_I__valid,
  input  reset,
  output [3:0] OpCode,
  output [1:0] OpCode_for_High,
  output [4:0] RF_Out_0_Sel,
  output [4:0] RF_Out_1_Sel,
  output [4:0] RF_Load_Sel,
  output Load_H_L,
  output [31:0] ALU_Input_0,
  output [31:0] ALU_Input_1,
  output H_L_out_Sel_for_RF,
  output [31:0] Input_0_for_RF,
  output [31:0] Input_1_for_RF,
  output jr,
  output J,
  output [31:0] jump_destiny,
  output beq,
  output bne,
  output blez,
  output bgtz,
  output [31:0] ctt_for_branch,
  output bltz,
  output tty_enable,
  output stop,
  output [6:0] tty_data,
  output push,
  output lw,
  output kbd_enable,
  output pop,
  output sw,
  output use_ID_address,
  output [31:0] Address_from_ID,
  output [31:0] RAM_input
);

  wire add, addi, \and , andi, div, divu, Especial, halt, I, kbd, mfhi, mflo, mult, mulu, nop, \nor , \or ,
       ori, R, rnd, slt, slti, sltiu, sltu, sub, tty, \xor , xori;
  wire [4:0] Rd, Rs, Rt;
  wire [15:0] \const ;
  wire [25:0] d_s;
  wire [31:0] Instruction_q;

  Register #(.width(32)) Instruction (.D(Data_From_RAM), .en(Inst_valid), .Q(Instruction_q), .clk(clk));  // open: clr
  Decoder decoder_1 (
    .R(R), .Rt(Rt), .I(I), .Especial(Especial), .Rs(Rs), .nop(nop), .Rd(Rd), .add(add), .\const (\const ),
    .sub(sub), .mult(mult), .destino_salto(d_s), .mulu(mulu), .div(div), .divu(divu), .slt(slt), .sltu(sltu),
    .\and (\and ), .\or (\or ), .\xor (\xor ), .\nor (\nor ), .pop(pop), .push(push), .mfhi(mfhi),
    .mflo(mflo), .jr(jr), .addi(addi), .sltiu(sltiu), .slti(slti), .ori(ori), .andi(andi), .xori(xori),
    .lw(lw), .sw(sw), .beq(beq), .bne(bne), .blez(blez), .bgtz(bgtz), .bltz(bltz), .J(J), .halt(halt),
    .tty(tty), .rnd(rnd), .kbd(kbd), .Instruction(Instruction_q));  // open: Output
  Execute_Instruction execute_instruction_1 (
    .Rt(Rt), .R(R), .I(I), .Rs(Rs), .Especial(Especial), .Rd(Rd), .\const (\const ), .destino_salto(d_s),
    .OpCode(OpCode), .ALU_High_Sel(OpCode_for_High), .Output0_Sel(RF_Out_0_Sel), .Output1_Sel(RF_Out_1_Sel),
    .Load_Sel(RF_Load_Sel), .Result_from_ALU(ALU_Result_L), .Result_from_ALU_High(ALU_High_value),
    .RF_Load__H_L(Load_H_L), .H_L_out_Sel(H_L_out_Sel_for_RF), .High_Low_value_from_RF(RF_Out_from_H_L),
    .Input_0__for_RF(Input_0_for_RF), .Rs_data(Rt_data), .Rt_data(Rs_data), .ALU_Input_0(ALU_Input_0),
    .ALU_Input_1(ALU_Input_1), .nop(nop), .add(add), .sub(sub), .mult(mult), .mulu(mulu), .div(div),
    .divu(divu), .slt(slt), .sltu(sltu), .\and (\and ), .\or (\or ), .\xor (\xor ), .\nor (\nor ), .pop(pop),
    .push(push), .mfhi(mfhi), .mflo(mflo), .jr(jr), .slti(slti), .addi(addi), .sltiu(sltiu), .ori(ori),
    .andi(andi), .xori(xori), .lw(lw), .sw(sw), .beq(beq), .bne(bne), .blez(blez), .bgtz(bgtz), .bltz(bltz),
    .J(J), .halt(halt), .tty(tty), .kbd(kbd), .Input_1__for_RF(Input_1_for_RF), .PC_value(PC_value),
    .jump_destiny(jump_destiny), .ctt_for_branch(ctt_for_branch), .stop(stop), .tty_enable(tty_enable),
    .tty_data(tty_data), .kbd_data(kbd_data), .kbd_available(kbd_available), .kbd_enable(kbd_enable),
    .M_I__result(Data_From_RAM), .Address_for_M_I(Address_from_ID), .M_I__valid(M_I__valid),
    .RAM_input(RAM_input), .use_ID_address(use_ID_address), .reset(reset), .rnd(rnd), .clk(clk));  // open: Output

  // Other names for the same wires on the sheet: Address_for_M_I[31:0] = Address_from_ID;
  //   ALU_High_OpCode_Sel[1:0] = OpCode_for_High; M_I__result_t[31:0] = Data_From_RAM; OpCode_for_ALU[3:0] = OpCode

  // Notes on the sheet:
  //   Input
  //   Outputs
endmodule

module CU (
  input  clk,
  input  start,
  input  [1:0] bank_selector,
  input  [1:0] RAM_data_sel,
  input  reset,
  input  stop,
  input  [6:0] tty_data,
  input  [3:0] Read_Time,
  input  tty_enable,
  input  [3:0] Write_Time,
  input  kbd_enable,
  input  [1:0] in_12,
  input  [31:0] RAM_Out_0,
  input  [31:0] RAM_Out_1,
  input  [31:0] RAM_Out_2,
  input  [31:0] RAM_Out_3,
  output [6:0] kbd_data,
  output [31:0] Instruction,
  output PC_enable,
  output kbd_available,
  output M_I__valid,
  output [31:0] RAM_data
);

  wire comparator_1_lt, comparator_2_eq, comparator_3_eq, CS_1, CS_2, CS_3, demultiplexer_1_out0,
       demultiplexer_1_out1, demultiplexer_4_out0, demultiplexer_5_out0, demultiplexer_6_out0,
       demultiplexer_7_out0, demultiplexer_8_out0, demultiplexer_9_out0, demultiplexer_10_out0,
       demultiplexer_11_out0, end_inst, end_inst_1, end_inst_2, end_inst_3, end_inst_4,
       get_data_from_ram_1_p10, Get_inst_q, IDLE_q, M_I__valid_t, nR_W_1, or_1_out, or_3_out, or_4_out,
       or_5_out, or_6_out, or_7_out, or_8_out, or_9_out, or_10_out, PC_enable_2, PC_enable_3, PC_enable_4,
       push, wait_a_cicle_2_q, wait_a_cicle_3_q, wait_a_cicle_4_q, wait_a_cicle_5_q, wait_a_cicle_q,
       wait_RT_2_q, wait_RT_3_q, wait_RT_q;
  wire [3:0] counter_1_q, counter_2_q, counter_3_q;
  wire [31:0] get_data_from_ram_1_p9;

  D_Flip_Flop #(.trigger("falling")) IDLE (.clk(clk), .D(or_1_out), .Q(IDLE_q), .preset(reset));  // open: Qn, en, reset
  or or_1 (or_1_out, demultiplexer_1_out0, end_inst);
  Demultiplexer demultiplexer_1 (
    .out0(demultiplexer_1_out0), .out1(demultiplexer_1_out1), .in(IDLE_q), .sel(start));  // open: en
  not not_1 (reset, IDLE_q);
  D_Flip_Flop #(.trigger("falling")) Get_inst (
    .clk(clk), .D(demultiplexer_1_out1), .Q(Get_inst_q), .reset(reset));  // open: Qn, preset, en
  // Get_Data_From_RAM get_data_from_ram_1: pin names not known; wires that end beside it: RAM_Out_3, clk, Get_inst_q, reset, RAM_Out_0, RAM_Out_1, RAM_Out_2, bank_selector, get_data_from_ram_1_p9, get_data_from_ram_1_p10
  Demultiplexer #(.width(32)) demultiplexer_2 (
    .out1(Instruction), .in(get_data_from_ram_1_p9), .sel(get_data_from_ram_1_p10));  // open: out0, en
  Demultiplexer #(.select(2)) demultiplexer_3 (
    .out0(CS_1), .out1(CS_2), .out2(push), .out3(PC_enable_4), .in(get_data_from_ram_1_p10), .sel(in_12));  // open: en
  or or_2 (end_inst, end_inst_1, end_inst_2, end_inst_3, end_inst_4);
  not not_2 (nR_W_1, CS_1);
  or or_3 (or_3_out, demultiplexer_4_out0, push);
  D_Flip_Flop #(.trigger("falling")) wait_RT (
    .clk(clk), .D(or_4_out), .Q(wait_RT_q), .reset(reset));  // open: Qn, preset, en
  or or_4 (or_4_out, demultiplexer_5_out0, CS_1);
  Demultiplexer demultiplexer_4 (
    .out0(demultiplexer_4_out0), .out1(CS_3), .in(1'b1), .sel(wait_a_cicle_q));  // open: en
  D_Flip_Flop #(.trigger("falling")) wait_a_cicle (
    .clk(clk), .D(or_3_out), .Q(wait_a_cicle_q), .reset(reset));  // open: Qn, preset, en
  Counter #(.width(4), .max('hf)) counter_1 (
    .count(wait_RT_q), .Q(counter_1_q), .clk(clk), .clr(reset));  // open: load, D, carry
  or or_5 (or_5_out, demultiplexer_7_out0, CS_2);
  Demultiplexer demultiplexer_5 (
    .out0(demultiplexer_5_out0), .out1(M_I__valid_t), .in(1'b1), .sel(comparator_1_lt));  // open: en
  Comparator #(.width(4)) comparator_1 (.a(Read_Time), .b(counter_1_q), .lt(comparator_1_lt));  // open: gt, eq
  or or_6 (or_6_out, demultiplexer_6_out0, PC_enable_4);
  Counter #(.width(4), .max('hf)) counter_2 (
    .count(wait_RT_2_q), .Q(counter_2_q), .clk(clk), .clr(reset));  // open: load, D, carry
  D_Flip_Flop #(.trigger("falling")) wait_RT_2 (
    .clk(clk), .D(or_5_out), .Q(wait_RT_2_q), .reset(reset));  // open: Qn, preset, en
  Demultiplexer demultiplexer_6 (
    .out0(demultiplexer_6_out0), .out1(end_inst_4), .in(1'b1), .sel(wait_a_cicle_2_q));  // open: en
  D_Flip_Flop #(.trigger("falling")) wait_a_cicle_2 (
    .clk(clk), .D(or_6_out), .Q(wait_a_cicle_2_q), .reset(reset));  // open: Qn, preset, en
  Demultiplexer demultiplexer_7 (
    .out0(demultiplexer_7_out0), .out1(PC_enable_2), .in(1'b1), .sel(comparator_2_eq));  // open: en
  Comparator #(.width(4)) comparator_2 (.a(Write_Time), .b(counter_2_q), .eq(comparator_2_eq));  // open: gt, lt
  D_Flip_Flop #(.trigger("falling")) wait_RT_3 (
    .clk(clk), .D(or_7_out), .Q(wait_RT_3_q), .reset(reset));  // open: Qn, preset, en
  or or_7 (or_7_out, demultiplexer_10_out0, CS_3);
  or or_8 (or_8_out, demultiplexer_8_out0, M_I__valid_t);
  Counter #(.width(4), .max('hf)) counter_3 (
    .count(wait_RT_3_q), .Q(counter_3_q), .clk(clk), .clr(reset));  // open: load, D, carry
  Demultiplexer demultiplexer_8 (
    .out0(demultiplexer_8_out0), .out1(end_inst_1), .in(1'b1), .sel(wait_a_cicle_3_q));  // open: en
  D_Flip_Flop #(.trigger("falling")) wait_a_cicle_3 (
    .clk(clk), .D(or_8_out), .Q(wait_a_cicle_3_q));  // open: Qn, preset, en, reset
  Demultiplexer demultiplexer_9 (
    .out0(demultiplexer_9_out0), .out1(end_inst_2), .in(1'b1), .sel(wait_a_cicle_4_q));  // open: en
  D_Flip_Flop #(.trigger("falling")) wait_a_cicle_4 (
    .clk(clk), .D(or_9_out), .Q(wait_a_cicle_4_q), .reset(reset));  // open: Qn, preset, en
  or or_9 (or_9_out, demultiplexer_9_out0, PC_enable_2);
  Demultiplexer demultiplexer_10 (
    .out0(demultiplexer_10_out0), .out1(PC_enable_3), .in(1'b1), .sel(comparator_3_eq));  // open: en
  Comparator #(.width(4)) comparator_3 (.a(Write_Time), .b(counter_3_q), .eq(comparator_3_eq));  // open: gt, lt
  or or_10 (or_10_out, demultiplexer_11_out0, PC_enable_3);
  Demultiplexer demultiplexer_11 (
    .out0(demultiplexer_11_out0), .out1(end_inst_3), .in(1'b1), .sel(wait_a_cicle_5_q));  // open: en
  D_Flip_Flop #(.trigger("falling")) wait_a_cicle_5 (
    .clk(clk), .D(or_10_out), .Q(wait_a_cicle_5_q), .reset(reset));  // open: Qn, preset, en
  or or_11 (M_I__valid, M_I__valid_t, CS_3);
  Multiplexer #(.select(2), .width(32)) multiplexer_1 (
    .in0(RAM_Out_0), .in1(RAM_Out_1), .in2(RAM_Out_2), .in3(RAM_Out_3),
    .out({RAM_data[7:0], RAM_data[15:8], RAM_data[23:16], RAM_data[31:24]}), .sel(RAM_data_sel),
    .en(M_I__valid_t));
  or or_12 (PC_enable, M_I__valid_t, PC_enable_2, PC_enable_3, PC_enable_4);

  // Other names for the same wires on the sheet: bank_sel[1:0] = bank_selector; inst[31:0] = Instruction;
  //   M_I__valid_1 = CS_3; nR_W_3 = CS_3; PC_enable_1 = M_I__valid_t; RAM_OUTPUT_0[31:0] = RAM_Out_0;
  //   RAM_OUTPUT_1[31:0] = RAM_Out_1; RAM_OUTPUT_2[31:0] = RAM_Out_2; RAM_OUTPUT_3[31:0] = RAM_Out_3; nR_W_2 = CS_2;
  //   sw = CS_2
endmodule

// Get_Data
module Get_Data_From_RAM (
  input  data_ready,
  input  [31:0] RAM_Out_0,
  input  [31:0] RAM_Out_1,
  input  [31:0] RAM_Out_2,
  input  [31:0] RAM_Out_3,
  input  [31:0] PC_value,
  input  [1:0] RAM_data_sel,
  output [31:0] RAM_data
);

  Multiplexer #(.select(2), .width(32)) multiplexer_1 (
    .in0(RAM_Out_0), .in1(RAM_Out_1), .in2(RAM_Out_2), .in3(RAM_Out_3),
    .out({RAM_data[7:0], RAM_data[15:8], RAM_data[23:16], RAM_data[31:24]}), .sel(RAM_data_sel),
    .en(data_ready));

  // Other names for the same wires on the sheet: RAM_OUTPUT_0[31:0] = RAM_Out_0; RAM_OUTPUT_1[31:0] = RAM_Out_1;
  //   RAM_OUTPUT_2[31:0] = RAM_Out_2; RAM_OUTPUT_3[31:0] = RAM_Out_3

  // Notes on the sheet:
  //   El enable debe ser que ya tiene la siguiente insrucción en la mano y disable es cuando termina con una instrucción
endmodule

module Execute_Instruction (
  input  nop,
  input  [4:0] Rt,
  input  R,
  input  add,
  input  I,
  input  [4:0] Rs,
  input  sub,
  input  Especial,
  input  mult,
  input  [4:0] Rd,
  input  mulu,
  input  [15:0] \const ,
  input  div,
  input  divu,
  input  slt,
  input  [25:0] destino_salto,
  input  sltu,
  input  \and ,
  input  \or ,
  input  \xor ,
  input  [31:0] Result_from_ALU,
  input  \nor ,
  input  pop,
  input  push,
  input  mfhi,
  input  [31:0] Result_from_ALU_High,
  input  mflo,
  input  jr,
  input  J,
  input  halt,
  input  [31:0] High_Low_value_from_RF,
  input  tty,
  input  rnd,
  input  kbd,
  input  addi,
  input  [31:0] Rs_data,
  input  sltiu,
  input  slti,
  input  ori,
  input  [31:0] Rt_data,
  input  andi,
  input  xori,
  input  lw,
  input  sw,
  input  beq,
  input  bne,
  input  blez,
  input  bgtz,
  input  bltz,
  input  [31:0] PC_value,
  input  [6:0] kbd_data,
  input  kbd_available,
  input  [31:0] M_I__result,
  input  M_I__valid,
  input  reset,
  input  clk,
  output [3:0] OpCode,
  output [1:0] Output,
  output [31:0] ALU_Input_0,
  output [1:0] ALU_High_Sel,
  output [4:0] Output0_Sel,
  output [4:0] Output1_Sel,
  output [31:0] ALU_Input_1,
  output [4:0] Load_Sel,
  output RF_Load__H_L,
  output H_L_out_Sel,
  output [31:0] Input_0__for_RF,
  output [31:0] Input_1__for_RF,
  output [31:0] jump_destiny,
  output [31:0] ctt_for_branch,
  output tty_enable,
  output stop,
  output [6:0] tty_data,
  output kbd_enable,
  output [31:0] Address_for_M_I,
  output [31:0] RAM_input,
  output use_ID_address
);

  wire Add_t, and_3_out, And_t, Enable_Load_Register, or_8_out, or_12_out, or_14_out, or_15_out, or_18_out,
       or_19_out, Or_t, Slt_t, Sltu_t, Sub_t, use_4, use_reg, Xor_t;
  wire [0:0] or_17_out;
  wire [31:0] and_1_out, and_2_out, bit_extender_1_out, bit_extender_2_out, bit_extender_3_out, kbd_data_32,
       M_I__operation, M_I__result_t, multiplexer_2_out, rnd_value;
  wire [31:30] _32_ctt;
  wire [31:31] not_1_out;

  Little_Endian_adjuster little_endian_adjuster_1 (.Input(M_I__result), .Output(M_I__result_t));
  Random #(.width(32)) random_1 (.clk(clk), .next(rnd), .out(rnd_value));  // open: clr
  assign bit_extender_1_out = {{31{1'b1}}, 1'b1};  // Bit_Extender bit_extender_1
  assign bit_extender_2_out = {{31{1'b1}}, 1'b1};  // Bit_Extender bit_extender_2
  not not_1 (not_1_out[31], kbd_available);
  or or_1 (Add_t, add, addi, pop, lw, sw);
  or or_2 (Slt_t, slt, slti);
  or or_3 (Sltu_t, sltu, sltiu);
  or or_4 (And_t, \and , andi);
  or or_5 (Or_t, \or , ori);
  or or_6 (Xor_t, \xor , xori);
  or or_7 (Sub_t, push, sub);
  or or_8 (or_8_out, pop, lw);
  assign bit_extender_3_out = {{25{1'b0}}, kbd_data};  // Bit_Extender bit_extender_3
  assign kbd_data_32 = bit_extender_3_out | {32{not_1_out[31]}};  // OR_Gate or_9, 32 bits wide
  assign and_1_out = ~bit_extender_1_out & Result_from_ALU;  // AND_Gate and_1, 32 bits wide
  // OR_Gate or_10 has open pins: in0=and_1_out, in1=and_2_out, out=open
  assign and_2_out = bit_extender_2_out & Rs_data;  // AND_Gate and_2, 32 bits wide
  Priority_Encoder #(.select(4)) priority_encoder_1 (
    .in0(Add_t), .in1(Sub_t), .in2(And_t), .in3(mult), .in4(mulu), .in5(div), .in6(divu), .in7(Or_t),
    .in8(\nor ), .in9(Xor_t), .in11(Slt_t), .in12(Sltu_t), .out(OpCode));  // open: in10, in13, in14, in15, gs, en_out, en_in
  or or_11 (use_4, pop, push);
  or or_12 (or_12_out, beq, bne);
  assign M_I__operation = {{31{pop}}, pop};  // Bit_Extender bit_extender_4
  and and_3 (and_3_out, M_I__valid, or_8_out);
  or or_13 (use_reg, R, or_12_out);
  or or_14 (or_14_out, blez, bgtz, bltz);
  Multiplexer #(.width(5), .enable("false")) multiplexer_1 (.in0(Rd), .in1(Rt), .out(Load_Sel), .sel(or_15_out));
  or or_15 (or_15_out, addi, sltiu, slti, andi, ori, xori, lw);
  Multiplexer #(.width(32), .enable("false")) multiplexer_2 (
    .in0(Result_from_ALU), .in1(M_I__result_t), .out(multiplexer_2_out), .sel(and_3_out));
  Priority_Encoder #(.select(2), .disabled(0)) priority_encoder_2 (
    .in0(I), .in1(use_reg), .in2(or_14_out), .in3(use_4), .out(Output));  // open: gs, en_out, en_in
  Priority_Encoder #(.select(2)) priority_encoder_3 (
    .in0(mult), .in1(mulu), .in2(div), .in3(divu), .out(ALU_High_Sel));  // open: gs, en_out, en_in
  assign {_32_ctt, ctt_for_branch[31:18]} = {{15{\const [15]}}, \const [15]};  // Bit_Extender bit_extender_5
  or or_16 (RF_Load__H_L, mult, mulu, div, divu);
  Multiplexer #(.select(2), .width(32), .disabled(0), .enable("false")) multiplexer_3 (
    .in0(multiplexer_2_out), .in1(High_Low_value_from_RF), .in2(rnd_value), .in3(kbd_data_32),
    .out(Input_0__for_RF), .sel({Especial, or_17_out[0]}));
  or or_17 (or_17_out[0], mfhi, kbd, mflo);
  Multiplexer #(.width(32), .enable("false")) multiplexer_4 (
    .in0(Result_from_ALU_High), .in1(Result_from_ALU), .out(Input_1__for_RF), .sel(M_I__valid));
  not not_2 (Enable_Load_Register, RF_Load__H_L);
  Multiplexer #(.width(32), .enable("false")) multiplexer_5 (
    .in0(Result_from_ALU), .in1(Rs_data), .out(Address_for_M_I), .sel(or_18_out));
  or or_18 (or_18_out, pop, push);
  Multiplexer #(.width(32), .enable("false")) multiplexer_6 (
    .in0(Rs_data), .in1(Rt_data), .out(RAM_input), .sel(or_19_out));
  or or_19 (or_19_out, sw, push);
  or or_20 (use_ID_address, sw, lw, pop, push);
  Multiplexer #(.select(2), .width(32), .enable("false")) multiplexer_7 (
    .in0({_32_ctt, ctt_for_branch[31:18], \const }), .in1(Rt_data), .in2({32{1'b0}}), .in3(32'h4),
    .out(ALU_Input_1), .sel(Output));

  assign ALU_Input_0 = Rs_data;
  assign ctt_for_branch[17:0] = {\const , 2'b00};
  assign H_L_out_Sel = mfhi;
  assign jump_destiny = {PC_value[31:28], destino_salto, 2'b00};
  assign kbd_enable = kbd;
  assign Output0_Sel = Rs;
  assign Output1_Sel = Rt;
  assign stop = halt;
  assign tty_data = Rs_data[6:0];
  assign tty_enable = tty;

  // Other names for the same wires on the sheet: _32_ctt[29:0] = {ctt_for_branch[31:18], \const };
  //   In1_Sel[1:0] = Output; Result_from_ALU_L[31:0] = Result_from_ALU

  // Notes on the sheet:
  //   Inputs
  //   Esto me podria llegar desde inst dec y que yo supiera la operacion para ALU, no la op especifica
endmodule

module Data_Path (
  input  clk,
  input  instruction_valid,
  input  [6:0] kbd_data,
  input  kbd_available,
  input  Load_Registers,
  input  Deactivate_nR_W,
  input  Load_SP,
  input  M_I__valid,
  input  reset,
  input  PC_Load,
  input  [31:0] RAM_Out_0,
  input  [31:0] RAM_Out_1,
  input  [31:0] RAM_Out_2,
  input  [31:0] RAM_Out_3,
  output [4:0] Output,
  output [31:0] Output_2,
  output [31:0] Output_3,
  output [31:0] RF_Output_0,
  output [31:0] Output_4,
  output [31:0] Output_5,
  output [31:0] RF_Output_1,
  output [31:0] Output_6,
  output [31:0] Output_7,
  output [31:0] RF_Out_from_H_L,
  output [31:0] Output_8,
  output [31:0] Output_9,
  output [6:0] tty_data,
  output [31:0] Output_10,
  output [2:0] OP_Code,
  output Read_from_memory,
  output Write_from_memory,
  output [31:0] Output_11,
  output [31:0] RAM_input,
  output [1:0] RAM_bank_sel,
  output [15:0] Address_forRAM,
  output [3:0] Mask
);

  wire and_1_out, beq, bgtz, blez, bltz, bne, H_L_Sel, halt, J, jr, kbd_enable, lw, or_1_out, or_2_out,
       or_3_out, pop, push, RF_Load_H_L, S_I0___I1, S_I0___I1_t, sw, tty_enable, use_ID_address;
  wire [1:0] ALU_High_OpCode_Sel;
  wire [3:0] OpCode;
  wire [4:0] RF_Enable_Sel, RF_Out_0_Sel;
  wire [31:0] Address_from_ID, ctt_for_branch, get_data_from_ram_1_ram_data, High_input, Input_0_for_RF_L,
       j_d, M_I__result, multiplexer_1_out, PC_value;

  Branch_Control branch_control_1 (
    .jump_destiny(j_d), .ctt_for_branch(ctt_for_branch), .jr(jr), .J(J), .beq(beq), .bne(bne), .blez(blez),
    .bgtz(bgtz), .bltz(bltz), .S_I0___I1(S_I0___I1), .S_I0___I1_2(S_I0___I1_t), .Rs_value(Output_2),
    .PC_value(PC_value), .PC_new_value(Output_10));
  Instruction_Decoder instruction_decoder_1 (
    .Data_From_RAM(Output_7), .Load_H_L(RF_Load_H_L), .RF_Load_Sel(RF_Enable_Sel), .RF_Out_1_Sel(Output),
    .RF_Out_0_Sel(RF_Out_0_Sel), .OpCode(OpCode), .OpCode_for_High(ALU_High_OpCode_Sel), .clk(clk),
    .ALU_Input_1(Output_9), .Rt_data(Output_2), .Rs_data(Output_3), .ALU_Input_0(Output_5),
    .ALU_Result_L(Output_6), .ALU_High_value(Output_8), .RF_Out_from_H_L(Output_4),
    .H_L_out_Sel_for_RF(H_L_Sel), .Input_0_for_RF(Input_0_for_RF_L), .Input_1_for_RF(High_input),
    .PC_value(PC_value), .jr(jr), .J(J), .beq(beq), .bne(bne), .jump_destiny(j_d), .blez(blez), .bgtz(bgtz),
    .bltz(bltz), .ctt_for_branch(ctt_for_branch), .tty_enable(tty_enable), .stop(halt), .tty_data(tty_data),
    .kbd_enable(kbd_enable), .kbd_data(kbd_data), .kbd_available(kbd_available), .pop(pop), .push(push),
    .M_I__result(M_I__result), .M_I__valid(M_I__valid), .use_ID_address(use_ID_address),
    .Address_from_ID(Address_from_ID), .RAM_input(RAM_input), .reset(reset), .Inst_valid(instruction_valid),
    .lw(lw), .sw(sw));
  PC pc_1 (.clk(clk), .enable(PC_Load), .reset(reset), .PC_new_value(Output_10), .PC_current_value(PC_value));
  or or_1 (or_1_out, instruction_valid, M_I__valid);
  Get_Data_From_RAM get_data_from_ram_1 (
    .RAM_data(get_data_from_ram_1_ram_data), .RAM_Out_0(RAM_Out_0), .RAM_Out_1(RAM_Out_1),
    .RAM_Out_2(RAM_Out_2), .RAM_Out_3(RAM_Out_3), .PC_value(PC_value), .data_ready(or_1_out),
    .RAM_data_sel(RAM_bank_sel));
  Little_Endian_adjuster little_endian_adjuster_1 (.Input(get_data_from_ram_1_ram_data), .Output(Output_7));
  ALU alu_1 (
    .Input_0(Output_5), .Input_1(Output_9), .OpCode(OpCode), .High_Sel(ALU_High_OpCode_Sel),
    .Result_Low(Output_6), .High(Output_8), ._1_bit_S_I0___I1(S_I0___I1), .S_I0___I1(S_I0___I1_t));  // open: Enable_H
  Register_File register_file_1 (
    .Output0_Sel(RF_Out_0_Sel), .Output1_Sel(Output), .Enable_Sel(RF_Enable_Sel), .Clock(clk),
    .in_5(Input_0_for_RF_L), .Enable_H_L(RF_Load_H_L), .H_L_Selector(H_L_Sel), .Output_0(Output_2),
    .H_L(Output_4), .Output_1(Output_3), .High_SP_Input(High_input), .reset(reset), .pop(pop),
    .M_I__valid(M_I__valid), .push(push), .Load_SP(Load_SP), .Load_Registers(Load_Registers));
  or or_2 (or_2_out, pop, lw);
  or or_3 (or_3_out, push, sw);
  Multiplexer #(.width(32)) multiplexer_1 (
    .in0(PC_value), .in1(Address_from_ID),
    .out({multiplexer_1_out[31:20], Address_forRAM, RAM_bank_sel, multiplexer_1_out[1:0]}), .sel(and_1_out));  // open: en
  and and_1 (and_1_out, use_ID_address, ~Deactivate_nR_W);  // AND_Gate
  and and_2 (Mask[0], ~RAM_bank_sel[0], ~RAM_bank_sel[1]);  // AND_Gate
  and and_3 (Mask[1], RAM_bank_sel[0], ~RAM_bank_sel[1]);  // AND_Gate
  and and_4 (Mask[2], ~RAM_bank_sel[0], RAM_bank_sel[1]);  // AND_Gate
  and and_5 (Mask[3], RAM_bank_sel[0], RAM_bank_sel[1]);
  or or_4 (OP_Code[0], tty_enable, kbd_enable, or_2_out);
  or or_5 (OP_Code[1], tty_enable, or_3_out);
  or or_6 (OP_Code[2], halt, kbd_enable);
  or or_7 (Write_from_memory, push, sw);
  or or_8 (Read_from_memory, pop, lw);

  assign Output_11 = Output_7;
  assign RF_Out_from_H_L = Output_4;
  assign RF_Output_0 = Output_2;
  assign RF_Output_1 = Output_3;

  // Other names for the same wires on the sheet: RAM_data_sel[1:0] = RAM_bank_sel;
  //   Address_for_RAM[15:0] = Address_forRAM; ALU_High[31:0] = Output_8; ALU_I0[31:0] = Output_5;
  //   ALU_I1[31:0] = Output_9; ALU_Result_L[31:0] = Output_6; PC_input[31:0] = Output_10; RAM_data[31:0] = Output_7;
  //   RAM_OUTPUT_0[31:0] = RAM_Out_0; RAM_OUTPUT_1[31:0] = RAM_Out_1; RAM_OUTPUT_2[31:0] = RAM_Out_2;
  //   RAM_OUTPUT_3[31:0] = RAM_Out_3; RF_Out_1_Sel[4:0] = Output

  // Notes on the sheet:
  //   Data Path
endmodule

module no_se (
  input  [4:0] Output0_Sel,
  input  [4:0] Output1_Sel,
  input  [4:0] Enable_Sel,
  input  [31:0] Input_for_RF,
  input  Clock,
  input  nop,
  input  Enable_H_L,
  input  add,
  input  H_L_Selector,
  input  sub,
  input  mult,
  input  in_12,
  input  [31:0] High_Input,
  input  mulu,
  input  div,
  input  divu,
  input  [31:0] _32_ctt,
  input  slt,
  input  sltu,
  input  \and ,
  input  \or ,
  input  [1:0] I1_Sel,
  input  \xor ,
  input  [1:0] ALU_High_Sel,
  input  \nor ,
  input  [3:0] OpCode,
  input  pop,
  input  push,
  input  reset,
  input  mfhi,
  input  mflo,
  input  jr,
  input  addi,
  input  sltiu,
  input  slti,
  output R,
  output [4:0] Rt,
  output I,
  output Especial,
  output [4:0] Rs,
  output nop_2,
  output [4:0] Rd,
  output add_2,
  output [15:0] \const ,
  output sub_2,
  output mult_2,
  output [25:0] destino_salto,
  output mulu_2,
  output div_2,
  output divu_2,
  output slt_2,
  output sltu_2,
  output and_2,
  output or_2,
  output xor_2,
  output nor_2,
  output pop_2,
  output push_2,
  output mfhi_2,
  output mflo_2,
  output jr_2,
  output addi_2,
  output sltiu_2,
  output slti_2,
  output ori,
  output andi,
  output xori,
  output lw,
  output sw,
  output beq,
  output bne,
  output blez,
  output bgtz,
  output bltz,
  output J,
  output halt,
  output tty,
  output rnd,
  output kbd
);

  // Pins of 4 and 6 bits meet at Input_for_RF[5:0]

  assign \const  = Input_for_RF[21:6];
  assign destino_salto = Input_for_RF[31:6];
  assign OpCode = Input_for_RF[3:0];
  assign Rd = Input_for_RF[21:17];
  assign Rs = Input_for_RF[31:27];
  assign Rt = Input_for_RF[26:22];

  // Other names for the same wires on the sheet: add_t = add_2; addi_t = addi_2; and_t = and_2; clk = Clock;
  //   div_t = div_2; divu_t = divu_2; H_L_Sel = H_L_Selector; High_In[31:0] = High_Input;
  //   FuncCode[5:0] = Input_for_RF[11:6]; jr_t = jr_2; mfhi_t = mfhi_2; mflo_t = mflo_2; mult_t = mult_2;
  //   mulu_t = mulu_2; nop_t = nop_2; nor_t = nor_2; or_t = or_2; pop_t = pop_2; push_t = push_2; slt_t = slt_2;
  //   slti_t = slti_2; sltiu_t = sltiu_2; sltu_t = sltu_2; sub_t = sub_2; xor_t = xor_2

  // Notes on the sheet:
  //   Inputs son senales de Execute Inst
endmodule

module Decoder (
  input  [31:0] Instruction,
  output nop,
  output [4:0] Rt,
  output add,
  output [4:0] Rs,
  output sub,
  output [4:0] Rd,
  output mult,
  output mulu,
  output [15:0] \const ,
  output div,
  output divu,
  output [25:0] destino_salto,
  output [5:0] Output,
  output slt,
  output sltu,
  output R,
  output \and ,
  output I,
  output \or ,
  output Especial,
  output \xor ,
  output \nor ,
  output pop,
  output push,
  output mfhi,
  output mflo,
  output jr,
  output addi,
  output sltiu,
  output slti,
  output ori,
  output andi,
  output xori,
  output lw,
  output sw,
  output beq,
  output bne,
  output blez,
  output bgtz,
  output bltz,
  output J,
  output halt,
  output tty,
  output rnd,
  output kbd
);

  wire _00, _01, _10, _11, and_1_out, and_11_out, and_12_out, and_29_out, and_32_out, and_33_out, and_34_out,
       and_47_out, comparator_2_eq, or_1_out, R_00, R_01, R_10;

  Comparator #(.width(6)) comparator_1 (.a(Output), .b(6'b000010), .eq(J));  // open: gt, lt
  Little_Endian_adjuster little_endian_adjuster_1 (
    .Input(Instruction), .Output({Output, destino_salto[25:16], \const }));
  Comparator #(.width(6)) comparator_2 (.a(Output), .b({6{1'b0}}), .eq(comparator_2_eq));  // open: gt, lt
  or or_1 (or_1_out, comparator_2_eq, and_1_out);
  and and_1 (and_1_out, Output[5], Output[4], Output[3]);
  and and_2 (Especial, and_1_out, Output[2]);
  and and_3 (I, ~or_1_out, ~J);  // AND_Gate
  and and_4 (R, or_1_out, ~Especial);  // AND_Gate
  and and_5 (_10, ~Output[0], I, Output[1]);  // AND_Gate
  and and_6 (_11, Output[0], I, Output[1]);
  and and_7 (_01, Output[0], I, ~Output[1]);  // AND_Gate
  and and_8 (_00, ~Output[0], I, ~Output[1]);  // AND_Gate
  and and_9 (mflo, ~\const [3], R_01, \const [1]);  // AND_Gate
  and and_10 (mfhi, ~\const [3], R_01, ~\const [1]);  // AND_Gate
  and and_11 (and_11_out, \const [3], R_01, ~\const [1]);  // AND_Gate
  and and_12 (and_12_out, \const [3], R_01, \const [1]);
  and and_13 (R_00, ~\const [4], R, ~\const [5]);  // AND_Gate
  and and_14 (R_10, ~\const [4], R, \const [5]);  // AND_Gate
  and and_15 (R_01, \const [4], R, ~\const [5]);  // AND_Gate
  and and_16 (divu, and_12_out, \const [0]);
  and and_17 (div, and_12_out, ~\const [0]);  // AND_Gate
  and and_18 (mulu, and_11_out, \const [0]);
  and and_19 (mult, and_11_out, ~\const [0]);  // AND_Gate
  and and_20 (addi, ~Output[2], _00, Output[3]);  // AND_Gate
  and and_21 (andi, Output[2], _00, Output[3]);
  and and_22 (beq, Output[2], _00, ~Output[3]);  // AND_Gate
  and and_23 (sltiu, ~Output[5], _11, Output[3]);  // AND_Gate
  and and_24 (sw, Output[5], _11, Output[3]);
  and and_25 (lw, Output[5], _11, ~Output[3]);  // AND_Gate
  and and_26 (bgtz, ~Output[5], _11, ~Output[3]);  // AND_Gate
  and and_27 (jr, ~\const [0], R_00, \const [3]);  // AND_Gate
  and and_28 (push, \const [0], R_00, ~\const [3]);  // AND_Gate
  and and_29 (and_29_out, ~\const [0], R_00, ~\const [3]);  // AND_Gate
  and and_30 (pop, and_29_out, Output[5]);
  and and_31 (nop, and_29_out, ~Output[5]);  // AND_Gate
  and and_32 (and_32_out, ~\const [3], R_10, ~\const [2]);  // AND_Gate
  and and_33 (and_33_out, \const [3], R_10, \const [1]);
  and and_34 (and_34_out, ~\const [3], R_10, \const [2]);  // AND_Gate
  and and_35 (\xor , \const [3], R_10, ~\const [1]);  // AND_Gate
  and and_36 (slti, ~Output[2], _10, Output[3]);  // AND_Gate
  and and_37 (xori, Output[2], _10, Output[3]);
  and and_38 (blez, Output[2], _10, ~Output[3]);  // AND_Gate
  and and_39 (bne, Output[2], _01, ~Output[3]);  // AND_Gate
  and and_40 (ori, Output[2], _01, Output[3]);
  and and_41 (bltz, ~Output[2], _01, ~Output[3]);  // AND_Gate
  and and_42 (sub, \const [1], and_32_out);
  and and_43 (add, ~\const [1], and_32_out);  // AND_Gate
  and and_44 (sltu, and_33_out, \const [0]);
  and and_45 (slt, ~\const [0], and_33_out);  // AND_Gate
  and and_46 (\and , and_34_out, ~\const [0]);  // AND_Gate
  and and_47 (and_47_out, and_34_out, \const [0]);
  and and_48 (\nor , and_47_out, \const [1]);
  and and_49 (\or , ~\const [1], and_47_out);  // AND_Gate
  and and_50 (halt, \const [0], Especial, \const [1]);
  and and_51 (tty, \const [0], Especial, ~\const [1]);  // AND_Gate
  and and_52 (rnd, ~\const [0], Especial, \const [1]);  // AND_Gate
  and and_53 (kbd, ~\const [0], Especial, ~\const [1]);  // AND_Gate

  assign destino_salto[15:0] = \const ;
  assign Rd = \const [15:11];
  assign Rs = destino_salto[25:21];
  assign Rt = destino_salto[20:16];

  // Other names for the same wires on the sheet: F_bit1 = \const [0]; FuncCode[5:0] = \const [5:0];
  //   F_bit2 = \const [1]; F_bit3 = \const [2]; F_bit4 = \const [3]; OpCode[5:0] = Output; Bit3 = Output[2];
  //   Bit4 = Output[3]; Bit6 = Output[5]

  // Notes on the sheet:
  //   Input
  //   Tipo I
  //   Tipo R
  //   Especiales
  //   Outputs
endmodule

module PC (
  input  clk,
  input  enable,
  input  reset,
  input  [31:0] PC_new_value,
  output [31:0] PC_current_value
);

  Register #(.width(32)) PC (.D(PC_new_value), .en(enable), .Q(PC_current_value), .clk(clk), .clr(reset));

  // Notes on the sheet:
  //   PC
endmodule

module Branch_Control (
  input  [31:0] jump_destiny,
  input  [31:0] ctt_for_branch,
  input  jr,
  input  J,
  input  beq,
  input  bne,
  input  blez,
  input  bgtz,
  input  bltz,
  input  S_I0___I1,
  input  S_I0___I1_2,
  input  [31:0] Rs_value,
  input  [31:0] PC_value,
  output [31:0] PC_new_value
);

  wire and_1_out, and_2_out, and_3_out, and_4_out, and_5_out, branch, or_1_out;
  wire [1:0] PC_selector;
  wire [31:0] PC___4, PC___4___ctt;

  or or_1 (or_1_out, S_I0___I1, S_I0___I1_2);
  and and_1 (and_1_out, beq, S_I0___I1_2);
  and and_2 (and_2_out, bne, ~S_I0___I1_2);  // AND_Gate
  and and_3 (and_3_out, blez, or_1_out);
  and and_4 (and_4_out, ~or_1_out, bgtz);  // AND_Gate
  and and_5 (and_5_out, bltz, S_I0___I1);
  or or_2 (branch, and_1_out, and_2_out, and_3_out, and_4_out, and_5_out);
  Adder #(.width(32)) adder_1 (.a(PC_value), .b(32'h4), .out(PC___4));  // open: cin, cout
  Priority_Encoder #(.select(2)) priority_encoder_1 (
    .in0(1'b1), .in1(branch), .in2(J), .in3(jr), .out(PC_selector));  // open: gs, en_out, en_in
  Multiplexer #(.select(2), .width(32)) multiplexer_1 (
    .in0(PC___4), .in1(PC___4___ctt), .in2(jump_destiny), .in3(Rs_value), .out(PC_new_value),
    .sel(PC_selector));  // open: en
  Adder #(.width(32)) adder_2 (.a(PC___4), .b(ctt_for_branch), .out(PC___4___ctt));  // open: cin, cout

  // Other names for the same wires on the sheet: S_I0___I1_t = S_I0___I1_2
endmodule

module exp (
  input  Clk,
  input  Reset,
  input  Push_or_pop,
  input  start,
  input  [1:0] Special,
  input  [3:0] RT,
  input  [3:0] WT,
  input  [1:0] OP_Sel,
  output out_9,
  output out_10,
  output halt,
  output out_12,
  output out_13,
  output update_PC,
  output CS
);

  wire comparator_1_eq, d_ff_3_q, d_ff_4_q, d_ff_5_q, d_ff_14_q, demultiplexer_1_out0, demultiplexer_1_out1,
       demultiplexer_2_out0, demultiplexer_2_out1, demultiplexer_3_out0, demultiplexer_3_out1,
       demultiplexer_3_out2, demultiplexer_3_out3, demultiplexer_4_out0, demultiplexer_4_out1,
       demultiplexer_5_out0, demultiplexer_6_out0, demultiplexer_6_out1, demultiplexer_7_out0,
       demultiplexer_7_out1, demultiplexer_8_out0, IDLE_q, M1, M2, M3, M4, or_1_out, or_2_out, or_3_out,
       or_6_out, or_7_out, or_8_out, or_10_out, R_W4, R_W5, R_W6, R_W7, reset_reg, reset_reg_0, reset_reg_1,
       RW_C1, RW_C2, undriven, Wait;
  wire [3:0] counter_1_q, RT____WT;

  D_Flip_Flop IDLE (.clk(Clk), .D(demultiplexer_1_out0), .Q(IDLE_q), .preset(or_1_out));  // open: Qn, en, reset
  or or_1 (or_1_out, Reset, ~start);  // OR_Gate
  Demultiplexer #(.enable("false")) demultiplexer_1 (
    .out0(demultiplexer_1_out0), .out1(demultiplexer_1_out1), .in(or_2_out), .sel(start));
  or or_2 (or_2_out, IDLE_q, reset_reg_1);
  or or_3 (or_3_out, demultiplexer_2_out0, demultiplexer_1_out1);
  D_Flip_Flop d_ff_1 (.clk(Clk), .D(or_3_out), .Q(M4), .reset(Reset));  // open: Qn, preset, en
  Demultiplexer #(.enable("false")) demultiplexer_2 (
    .out0(demultiplexer_2_out0), .out1(demultiplexer_2_out1), .in(M4), .sel(Wait));
  D_Flip_Flop d_ff_2 (.clk(Clk), .D(demultiplexer_2_out1), .Q(reset_reg_0), .reset(Reset));  // open: Qn, preset, en
  Demultiplexer #(.select(2), .enable("false")) demultiplexer_3 (
    .out0(demultiplexer_3_out0), .out1(demultiplexer_3_out1), .out2(demultiplexer_3_out2),
    .out3(demultiplexer_3_out3), .in(reset_reg_0), .sel(OP_Sel));
  or or_4 (reset_reg, reset_reg_0, reset_reg_1);
  Demultiplexer #(.enable("false")) demultiplexer_4 (
    .out0(demultiplexer_4_out0), .out1(demultiplexer_4_out1), .in(demultiplexer_3_out2), .sel(Push_or_pop));
  Demultiplexer #(.select(2), .enable("false")) demultiplexer_5 (
    .out0(demultiplexer_5_out0), .out1(out_12), .out2(R_W6), .out3(R_W7), .in(demultiplexer_3_out3),
    .sel(Special));
  or or_5 (CS, M1, M3, M2, M4);
  D_Flip_Flop d_ff_3 (.clk(Clk), .D(undriven), .Q(d_ff_3_q), .reset(Reset));  // open: Qn, preset, en
  D_Flip_Flop d_ff_4 (.clk(Clk), .D(demultiplexer_4_out0), .Q(d_ff_4_q), .reset(Reset));  // open: Qn, preset, en
  D_Flip_Flop d_ff_5 (.clk(Clk), .D(out_12), .Q(d_ff_5_q), .reset(Reset));  // open: Qn, preset, en
  D_Flip_Flop d_ff_6 (.clk(Clk), .D(or_6_out), .Q(M1), .reset(Reset));  // open: Qn, preset, en
  or or_6 (or_6_out, demultiplexer_6_out0, demultiplexer_3_out1);
  or or_7 (or_7_out, demultiplexer_8_out0, demultiplexer_4_out1);
  Demultiplexer #(.enable("false")) demultiplexer_6 (
    .out0(demultiplexer_6_out0), .out1(demultiplexer_6_out1), .in(M1), .sel(Wait));
  D_Flip_Flop d_ff_7 (.clk(Clk), .D(or_8_out), .Q(M2), .reset(Reset));  // open: Qn, preset, en
  or or_8 (or_8_out, demultiplexer_7_out0, d_ff_4_q);
  D_Flip_Flop d_ff_8 (.clk(Clk), .D(or_7_out), .Q(M3), .reset(Reset));  // open: Qn, preset, en
  D_Flip_Flop d_ff_9 (
    .clk(Clk), .D(demultiplexer_5_out0), .Q(halt), .preset(demultiplexer_5_out0), .en(demultiplexer_5_out0),
    .reset(Reset));  // open: Qn
  D_Flip_Flop d_ff_10 (.clk(Clk), .D(R_W7), .Q(out_13), .reset(Reset));  // open: Qn, preset, en
  or or_9 (out_9, M2, M1);
  Demultiplexer #(.enable("false")) demultiplexer_7 (
    .out0(demultiplexer_7_out0), .out1(demultiplexer_7_out1), .in(M2), .sel(Wait));
  Demultiplexer #(.enable("false")) demultiplexer_8 (.out0(demultiplexer_8_out0), .out1(R_W4), .in(M3), .sel(Wait));
  or or_10 (or_10_out, d_ff_5_q, R_W6, out_13);
  D_Flip_Flop d_ff_11 (.clk(Clk), .D(demultiplexer_6_out1), .Q(RW_C1), .reset(Reset));  // open: Qn, preset, en
  Multiplexer #(.width(4), .enable("false")) multiplexer_1 (.in0(RT), .in1(WT), .out(RT____WT), .sel(out_9));
  D_Flip_Flop d_ff_12 (.clk(Clk), .D(demultiplexer_7_out1), .Q(RW_C2), .reset(Reset));  // open: Qn, preset, en
  D_Flip_Flop d_ff_13 (.clk(Clk), .D(R_W4), .Q(R_W5), .reset(Reset));  // open: Qn, preset, en
  D_Flip_Flop d_ff_14 (.clk(Clk), .D(CS), .Q(d_ff_14_q), .reset(Reset));  // open: Qn, preset, en
  or or_11 (update_PC, demultiplexer_3_out0, RW_C1, RW_C2, R_W5, or_10_out);
  Comparator #(.width(4)) comparator_1 (.a(RT), .b(counter_1_q), .eq(comparator_1_eq));  // open: gt, lt
  Counter #(.width(4), .max('hf)) counter_1 (
    .count(d_ff_14_q), .Q(counter_1_q), .clk(Clk), .clr(reset_reg));  // open: load, D, carry
  D_Flip_Flop END (.clk(Clk), .D(update_PC), .Q(reset_reg_1), .reset(Reset));  // open: Qn, preset, en
  and and_1 (Wait, comparator_1_eq, d_ff_14_q);
  or or_12 (out_10, RW_C1, RW_C2);

  // Other names for the same wires on the sheet: EKbd = out_13; LTTY = out_12; P_pop = Push_or_pop; PC = update_PC;
  //   R_W_RAM = M1; R_W_RAM_1 = M2; R_W_RAM_2 = M4; reset_reg3 = M3; RW_RAM = out_9; Sadr_10 = R_W5; SD_01 = R_W6;
  //   SD_10 = R_W7; SD_11 = R_W4

  // Notes on the sheet:
  //   Input Data
  //   other
  //   Store
  //   Push
  //   Pop/lw
  //   Halt
  //   TTY
  //   Rnd
  //   Kbd
  //   Branch
  //   |
  //   |
  //   |
  //   |
  //   |
  //   |
  //   |
  //   |
  //   |
  //   |
  //   |
  //   |
  //   |
  //   |
  //   |
  //   |
  //   |
  //   |
  //   |
  //   |
  //   |
  //   |
  //   |
  //   |
  //   |
  //   Wait for RT or WT
  //   ____________________________________
  //   Output Data
  //   |
  //   |
  //   |
  //   |
  //   |
  //   |
  //   |
  //   |
  //   |
  //   |
  //   |
  //   |
  //   |
  //   |
  //   |
  //   |
  //   |
  //   |
  //   |
  //   |
  //   |
  //   |
  //   |
  //   |
  //   |
endmodule

module Wait_RT_WT (
  input  start,
  input  [3:0] Write_Time,
  input  clk,
  input  [3:0] Read_Time,
  input  RT_or_WT_sel,
  output \end 
);

  wire CS1, CS2, demultiplexer_1_out0, demultiplexer_2_out0, demultiplexer_2_out1, demultiplexer_3_out1,
       END_q, IDLE_q, load_counter, or_1_out, reset, RT_passed;
  wire [3:0] counter_1_q, time_to_wait;

  or or_1 (or_1_out, demultiplexer_1_out0, demultiplexer_3_out1);
  Demultiplexer demultiplexer_1 (.out0(demultiplexer_1_out0), .out1(reset), .in(IDLE_q), .sel(start));  // open: en
  D_Flip_Flop #(.trigger("falling")) IDLE (.clk(clk), .D(or_1_out), .Q(IDLE_q), .preset(start));  // open: Qn, en, reset
  or or_2 (CS1, demultiplexer_2_out0, reset);
  D_Flip_Flop #(.trigger("falling")) wait_RT (.clk(clk), .D(CS1), .Q(load_counter));  // open: Qn, preset, en, reset
  Counter #(.width(4), .max('hf)) counter_1 (
    .count(load_counter), .Q(counter_1_q), .clk(clk), .clr(reset));  // open: load, D, carry
  Multiplexer #(.width(4)) multiplexer_1 (
    .in0(Write_Time), .in1(Read_Time), .out(time_to_wait), .sel(RT_or_WT_sel));  // open: en
  Demultiplexer demultiplexer_2 (
    .out0(demultiplexer_2_out0), .out1(demultiplexer_2_out1), .in(load_counter), .sel(RT_passed));  // open: en
  Comparator #(.width(4)) comparator_1 (.a(time_to_wait), .b(counter_1_q), .eq(RT_passed));  // open: gt, lt
  D_Flip_Flop #(.trigger("falling")) u_END (.clk(clk), .D(CS2), .Q(END_q));  // open: Qn, preset, en, reset
  or or_3 (CS2, \end , demultiplexer_2_out1);
  Demultiplexer demultiplexer_3 (.out0(\end ), .out1(demultiplexer_3_out1), .in(END_q), .sel(start));  // open: en
endmodule

module CU_2_0 (
  input  clk,
  input  halt,
  input  stop,
  input  [6:0] tty_data,
  input  tty_enable,
  input  kbd_enable,
  input  start,
  input  reset,
  input  [3:0] Read_Time,
  input  [3:0] Write_Time,
  input  in_11,
  input  in_12,
  input  [1:0] bank_selector,
  input  in_14,
  input  [1:0] RAM_data_sel,
  input  [1:0] OP_sel,
  input  [31:0] RAM_Out_0,
  input  [31:0] RAM_Out_1,
  input  [31:0] RAM_Out_2,
  input  [31:0] RAM_Out_3,
  output [31:0] RAM_data,
  output halt_2
);

  wire demultiplexer_1_out0, demultiplexer_2_out0, demultiplexer_4_out0, demultiplexer_4_out1,
       demultiplexer_5_out0, HALT_q, IDLE_q, not_1_out, or_1_out, or_4_out, other, pop_lw, pop_lw_end, push,
       Read, reading_finished_1, start_waiting, sw, undriven, undriven_2, wait_over, WAIT_q;

  or or_1 (or_1_out, demultiplexer_1_out0, demultiplexer_5_out0);
  Demultiplexer demultiplexer_1 (
    .out0(demultiplexer_1_out0), .out1(start_waiting), .in(IDLE_q), .sel(start));  // open: en
  D_Flip_Flop #(.trigger("falling")) IDLE (
    .clk(clk), .D(or_1_out), .Q(IDLE_q), .preset(not_1_out));  // open: Qn, en, reset
  not not_1 (not_1_out, start);
  // OR_Gate or_2 has open pins: in0=pop_lw_end, in1=in_11, in2=in_12, in3=in_14, out=open
  or or_3 (Read, demultiplexer_2_out0, start_waiting);
  D_Flip_Flop #(.trigger("falling")) WAIT (.clk(clk), .D(Read), .Q(WAIT_q), .en(start));  // open: Qn, preset, reset
  Demultiplexer demultiplexer_2 (
    .out0(demultiplexer_2_out0), .out1(reading_finished_1), .in(WAIT_q), .sel(wait_over));  // open: en
  Wait_RT_WT wait_rt_wt_1 (
    .start(start_waiting), .Write_Time(Write_Time), .clk(clk), .Read_Time(Read_Time), .RT_or_WT_sel(Read),
    .\end (wait_over));
  Demultiplexer #(.select(2)) demultiplexer_3 (
    .out0(pop_lw), .out1(sw), .out2(push), .out3(other), .in(demultiplexer_4_out0), .sel(OP_sel));  // open: en
  Demultiplexer demultiplexer_4 (
    .out0(demultiplexer_4_out0), .out1(demultiplexer_4_out1), .in(reading_finished_1), .sel(halt));  // open: en
  or or_4 (or_4_out, undriven_2, undriven);
  Demultiplexer demultiplexer_5 (.out0(demultiplexer_5_out0), .out1(halt_2), .in(HALT_q), .sel(start));  // open: en
  D_Flip_Flop #(.trigger("falling")) u_HALT (
    .clk(clk), .D(or_4_out), .Q(HALT_q), .en(start));  // open: Qn, preset, reset
  Multiplexer #(.select(2), .width(32)) multiplexer_1 (
    .in0(RAM_Out_0), .in1(RAM_Out_1), .in2(RAM_Out_2), .in3(RAM_Out_3),
    .out({RAM_data[7:0], RAM_data[15:8], RAM_data[23:16], RAM_data[31:24]}), .sel(RAM_data_sel),
    .en(reading_finished_1));

  // Other names for the same wires on the sheet: bank_sel[1:0] = bank_selector; other_end = in_14; push_end = in_12;
  //   RAM_OUTPUT_0[31:0] = RAM_Out_0; RAM_OUTPUT_1[31:0] = RAM_Out_1; RAM_OUTPUT_2[31:0] = RAM_Out_2;
  //   RAM_OUTPUT_3[31:0] = RAM_Out_3; sw_end = in_11
endmodule

module each_inst_for_CU (
  input  [3:0] WT,
  input  [3:0] RT,
  input  clk,
  input  pop_lw,
  input  sw,
  input  push,
  input  other,
  output \end 
);

  wire demultiplexer_1_out0, demultiplexer_2_out0, demultiplexer_3_out0, END_q, IDLE_q, M_I__valid,
       not_1_out, not_2_out, or_1_out, or_3_out, Read, start_waiting, wait_over, WAIT_q;

  or or_1 (or_1_out, demultiplexer_1_out0, \end );
  D_Flip_Flop #(.trigger("falling")) IDLE (
    .clk(clk), .D(or_1_out), .Q(IDLE_q), .preset(not_1_out));  // open: Qn, en, reset
  Demultiplexer demultiplexer_1 (
    .out0(demultiplexer_1_out0), .out1(start_waiting), .in(IDLE_q), .sel(pop_lw));  // open: en
  not not_1 (not_1_out, pop_lw);
  Wait_RT_WT wait_rt_wt_1 (
    .start(start_waiting), .Write_Time(WT), .clk(clk), .Read_Time(RT), .RT_or_WT_sel(Read), .\end (wait_over));
  or or_2 (Read, demultiplexer_2_out0, start_waiting);
  D_Flip_Flop #(.trigger("falling")) WAIT (.clk(clk), .D(Read), .Q(WAIT_q), .en(pop_lw));  // open: Qn, preset, reset
  Demultiplexer demultiplexer_2 (
    .out0(demultiplexer_2_out0), .out1(M_I__valid), .in(WAIT_q), .sel(wait_over));  // open: en
  D_Flip_Flop #(.trigger("falling")) u_END (
    .clk(clk), .D(or_3_out), .Q(END_q), .en(pop_lw));  // open: Qn, preset, reset
  or or_3 (or_3_out, demultiplexer_3_out0, M_I__valid);
  Demultiplexer demultiplexer_3 (.out0(demultiplexer_3_out0), .out1(\end ), .in(END_q), .sel(not_2_out));  // open: en
  not not_2 (not_2_out, pop_lw);

  // Other names for the same wires on the sheet: pop_lw_end = \end ; Read_Time[3:0] = RT;
  //   reading_finished = M_I__valid; Write_Time[3:0] = WT
endmodule

module CU_3_0 (
  input  in_1,
  input  in_2,
  input  in_3,
  input  in_4,
  input  in_5,
  input  in_6,
  input  [1:0] in_7,
  input  [3:0] in_8,
  input  [3:0] in_9,
  input  [1:0] in_10,
  output [1:0] out_11,
  output [1:0] out_12,
  output out_13,
  output out_14,
  output out_15,
  output out_16,
  output out_17,
  output out_18,
  output out_19,
  output out_20
);

  wire and_1_out, d_ff_1_q, d_ff_2_q, d_ff_3_q, d_ff_4_q, d_ff_14_q, demultiplexer_1_out0,
       demultiplexer_1_out1, demultiplexer_2_out0, demultiplexer_2_out1, demultiplexer_2_out2,
       demultiplexer_2_out3, demultiplexer_3_out0, demultiplexer_3_out1, demultiplexer_4_out1,
       demultiplexer_5_out0, demultiplexer_6_out0, demultiplexer_6_out1, demultiplexer_7_out0,
       demultiplexer_8_out0, demultiplexer_8_out1, demultiplexer_9_out0, END_q, IDLE_q, M1, M2, M3, M4,
       nor_1_out, or_1_out, or_3_out, or_8_out, or_9_out, or_10_out, or_11_out, or_13_out, R_W1, R_W2, R_W3,
       R_W4, R_W5, R_W6, R_W7, RW_C1, RW_C2, Sadr_00_____Sadr_01, undriven, Wait;
  wire [3:0] counter_1_q, RT____WT;

  D_Flip_Flop IDLE (.clk(in_2), .D(demultiplexer_1_out0), .Q(IDLE_q), .preset(or_1_out));  // open: Qn, en, reset
  or or_1 (or_1_out, in_1, ~in_5);  // OR_Gate
  or or_2 (out_11[1], R_W3, R_W5);
  Demultiplexer #(.enable("false")) demultiplexer_1 (
    .out0(demultiplexer_1_out0), .out1(demultiplexer_1_out1), .in(or_3_out), .sel(in_5));
  or or_3 (or_3_out, IDLE_q, END_q);
  and and_1 (and_1_out, Sadr_00_____Sadr_01, in_6);
  or or_4 (out_11[0], and_1_out, R_W2);
  D_Flip_Flop d_ff_1 (.clk(in_2), .D(demultiplexer_1_out1), .Q(d_ff_1_q), .reset(in_1));  // open: Qn, preset, en
  Demultiplexer #(.select(2), .enable("false")) demultiplexer_2 (
    .out0(demultiplexer_2_out0), .out1(demultiplexer_2_out1), .out2(demultiplexer_2_out2),
    .out3(demultiplexer_2_out3), .in(d_ff_1_q), .sel(in_10));
  Demultiplexer #(.enable("false")) demultiplexer_3 (
    .out0(demultiplexer_3_out0), .out1(demultiplexer_3_out1), .in(undriven), .sel(in_4));
  Demultiplexer #(.enable("false")) demultiplexer_4 (
    .out0(R_W3), .out1(demultiplexer_4_out1), .in(demultiplexer_2_out1), .sel(in_3));
  Demultiplexer #(.select(2), .enable("false")) demultiplexer_5 (
    .out0(demultiplexer_5_out0), .out1(out_17), .out2(R_W6), .out3(R_W7), .in(demultiplexer_2_out2),
    .sel(in_7));
  or or_5 (out_20, M3, M1, M2, M4);
  D_Flip_Flop d_ff_2 (.clk(in_2), .D(demultiplexer_2_out3), .Q(d_ff_2_q), .reset(in_1));  // open: Qn, preset, en
  or or_6 (out_12[0], R_W4, R_W6, R_W2);
  or or_7 (out_12[1], R_W4, R_W7, R_W2);
  D_Flip_Flop d_ff_3 (.clk(in_2), .D(R_W3), .Q(d_ff_3_q), .reset(in_1));  // open: Qn, preset, en
  D_Flip_Flop d_ff_4 (.clk(in_2), .D(out_17), .Q(d_ff_4_q), .reset(in_1));  // open: Qn, preset, en
  D_Flip_Flop d_ff_5 (.clk(in_2), .D(or_8_out), .Q(M1), .reset(in_1));  // open: Qn, preset, en
  or or_8 (or_8_out, demultiplexer_6_out0, demultiplexer_3_out0);
  or or_9 (or_9_out, demultiplexer_9_out0, demultiplexer_4_out1);
  Demultiplexer #(.enable("false")) demultiplexer_6 (
    .out0(demultiplexer_6_out0), .out1(demultiplexer_6_out1), .in(M1), .sel(Wait));
  D_Flip_Flop d_ff_6 (.clk(in_2), .D(or_10_out), .Q(M2), .reset(in_1));  // open: Qn, preset, en
  or or_10 (or_10_out, demultiplexer_7_out0, demultiplexer_3_out1);
  D_Flip_Flop d_ff_7 (.clk(in_2), .D(or_11_out), .Q(M3), .reset(in_1));  // open: Qn, preset, en
  or or_11 (or_11_out, demultiplexer_8_out0, d_ff_3_q);
  D_Flip_Flop d_ff_8 (.clk(in_2), .D(or_9_out), .Q(M4), .reset(in_1));  // open: Qn, preset, en
  D_Flip_Flop d_ff_9 (
    .clk(in_2), .D(demultiplexer_5_out0), .Q(out_16), .preset(demultiplexer_5_out0),
    .en(demultiplexer_5_out0), .reset(in_1));  // open: Qn
  D_Flip_Flop d_ff_10 (.clk(in_2), .D(R_W7), .Q(out_18), .reset(in_1));  // open: Qn, preset, en
  or or_12 (out_13, M3, M1);
  Demultiplexer #(.enable("false")) demultiplexer_7 (.out0(demultiplexer_7_out0), .out1(R_W2), .in(M2), .sel(Wait));
  Demultiplexer #(.enable("false")) demultiplexer_8 (
    .out0(demultiplexer_8_out0), .out1(demultiplexer_8_out1), .in(M3), .sel(Wait));
  Demultiplexer #(.enable("false")) demultiplexer_9 (.out0(demultiplexer_9_out0), .out1(R_W4), .in(M4), .sel(Wait));
  or or_13 (or_13_out, d_ff_4_q, R_W6, out_18);
  D_Flip_Flop d_ff_11 (.clk(in_2), .D(demultiplexer_6_out1), .Q(RW_C1), .reset(in_1));  // open: Qn, preset, en
  Multiplexer #(.width(4), .enable("false")) multiplexer_1 (.in0(in_8), .in1(in_9), .out(RT____WT), .sel(out_13));
  D_Flip_Flop d_ff_12 (.clk(in_2), .D(demultiplexer_8_out1), .Q(RW_C2), .reset(in_1));  // open: Qn, preset, en
  D_Flip_Flop d_ff_13 (.clk(in_2), .D(R_W4), .Q(R_W5), .reset(in_1));  // open: Qn, preset, en
  D_Flip_Flop d_ff_14 (.clk(in_2), .D(out_20), .Q(d_ff_14_q), .reset(in_1));  // open: Qn, preset, en
  or or_14 (out_19, demultiplexer_2_out0, RW_C1, R_W2, RW_C2, R_W5, or_13_out, d_ff_2_q);
  Counter #(.width(4), .max('hf)) counter_1 (
    .load(out_20), .D(RT____WT), .count(d_ff_14_q), .Q(counter_1_q), .clk(in_2));  // open: carry, clr
  D_Flip_Flop END (.clk(in_2), .D(out_19), .Q(END_q), .reset(in_1));  // open: Qn, preset, en
  nor nor_1 (nor_1_out, counter_1_q[0], counter_1_q[1], counter_1_q[2], counter_1_q[3]);
  and and_2 (Wait, nor_1_out, d_ff_14_q);
  or or_15 (out_14, R_W6, R_W1, R_W4, R_W2, R_W5, R_W3, R_W7);
  or or_16 (out_15, RW_C1, RW_C2);

  // Other names for the same wires on the sheet: Clk = in_2; CS = out_20; EKbd = out_18; I_type = in_6; L_S = in_4;
  //   LTTY = out_17; Op_sel[1:0] = in_10; P_pop = in_3; PC = out_19; R_W_RAM = M1; R_W_RAM_1 = M3; Reset = in_1;
  //   RT[3:0] = in_8; RW_RAM = out_13; S_Adrress[1:0] = out_11; S_Data[1:0] = out_12; Sadr_01 = R_W2;
  //   SD_11__prime = R_W2; Sadr_10 = R_W5; Sadr_10__prime = R_W3; SD_01 = R_W6; SD_10 = R_W7; SD_11 = R_W4;
  //   Special[1:0] = in_7; start = in_5; WT[3:0] = in_9

  // Notes on the sheet:
  //   Input Data
  //   other
  //   Store
  //   Load
  //   Push
  //   Pop
  //   Halt
  //   TTY
  //   Rnd
  //   Kbd
  //   Branch
  //   |
  //   |
  //   |
  //   |
  //   |
  //   |
  //   |
  //   |
  //   |
  //   |
  //   |
  //   |
  //   |
  //   |
  //   |
  //   |
  //   |
  //   |
  //   |
  //   |
  //   |
  //   |
  //   |
  //   |
  //   |
  //   Wait for RT or WT
  //   ____________________________________
  //   Output Data
  //   |
  //   |
  //   |
  //   |
  //   |
  //   |
  //   |
  //   |
  //   |
  //   |
  //   |
  //   |
  //   |
  //   |
  //   |
  //   |
  //   |
  //   |
  //   |
  //   |
  //   |
  //   |
  //   |
  //   |
  //   |
endmodule

module CU_4 (
  input  clk,
  input  Reset,
  input  [3:0] RT,
  input  [3:0] WT,
  input  [2:0] OP_Sel,
  input  Cached,
  output CS,
  output pop_lw_ready,
  output Inst_ready,
  output PC_load,
  output M_I__valid,
  output Load_SP,
  output tty_enable,
  output kbd_enable,
  output Load_Registers,
  output Deactivate_nR_W,
  output stop,
  output Invalidate_cache_address
);

  wire and_1_out, and_2_out, comparator_1_eq, CS1, CS2, CS3, CS5, Deactivate_nR_W_2, demultiplexer_1_out0,
       demultiplexer_1_out1, demultiplexer_1_out3, demultiplexer_1_out4, demultiplexer_2_out0,
       demultiplexer_2_out1, demultiplexer_3_out1, END_q, Halt_q, IDLE_q, not_1_out, or_1_out, or_2_out,
       or_3_out, or_4_out, or_5_out, or_6_out, Wait_PC_load_q;
  wire [3:0] counter_1_q;

  or or_1 (or_1_out, demultiplexer_2_out0, END_q);
  D_Flip_Flop #(.trigger("falling")) Wait_PC_load (
    .clk(clk), .D(Inst_ready), .Q(Wait_PC_load_q), .reset(Reset));  // open: Qn, preset, en
  Demultiplexer #(.select(3), .enable("false")) demultiplexer_1 (
    .out0(demultiplexer_1_out0), .out1(demultiplexer_1_out1), .out2(Load_SP), .out3(demultiplexer_1_out3),
    .out4(demultiplexer_1_out4), .out5(kbd_enable), .in(Wait_PC_load_q), .sel(OP_Sel));  // open: out6, out7
  D_Flip_Flop #(.trigger("falling")) IDLE (.clk(clk), .D(or_1_out), .Q(IDLE_q), .preset(Reset));  // open: Qn, en, reset
  Demultiplexer #(.enable("false")) demultiplexer_2 (
    .out0(demultiplexer_2_out0), .out1(demultiplexer_2_out1), .in(IDLE_q), .sel(not_1_out));
  not not_1 (not_1_out, Reset);
  and and_1 (and_1_out, ~comparator_1_eq, CS1);  // AND_Gate
  or or_2 (or_2_out, and_1_out, demultiplexer_2_out1);
  Wait_RT wait_rt_1 (.clk(clk), .RT(RT), .Cached(Cached), .start(demultiplexer_1_out1), .CS(CS2), .ready(pop_lw_ready));
  or or_3 (or_3_out, stop, demultiplexer_1_out4);
  Demultiplexer #(.enable("false")) demultiplexer_3 (
    .out0(CS1), .out1(demultiplexer_3_out1), .in(Deactivate_nR_W_2), .sel(and_2_out));
  D_Flip_Flop #(.trigger("falling")) Read_Inst (
    .clk(clk), .D(or_2_out), .Q(Deactivate_nR_W_2), .reset(Reset));  // open: Qn, preset, en
  Demultiplexer demultiplexer_4 (.out0(stop), .in(Halt_q), .sel(Reset));  // open: out1, en
  D_Flip_Flop #(.trigger("falling")) Halt (.clk(clk), .D(or_3_out), .Q(Halt_q));  // open: Qn, preset, en, reset
  and and_2 (and_2_out, Deactivate_nR_W_2, Cached);
  Wait_WT wait_wt_1 (
    .in_1(clk), .WT(WT), .start(Load_SP), .CS(CS3), .ready(CS5),
    .Invalidate_cache_address(Invalidate_cache_address));
  Comparator #(.width(4)) comparator_1 (.a(RT), .b(counter_1_q), .eq(comparator_1_eq));  // open: gt, lt
  Counter #(.width(4), .max('hf)) counter_1 (
    .count(CS1), .Q(counter_1_q), .clk(clk), .clr(or_4_out));  // open: load, D, carry
  or or_4 (or_4_out, Inst_ready, Reset);
  D_Flip_Flop #(.trigger("falling")) Wait_PC_load_2 (
    .clk(clk), .D(demultiplexer_1_out3), .Q(tty_enable), .reset(Reset));  // open: Qn, preset, en
  or or_5 (or_5_out, demultiplexer_3_out1, comparator_1_eq);
  D_Flip_Flop #(.trigger("falling")) d_ff_1 (
    .clk(clk), .D(or_5_out), .Q(Inst_ready), .reset(Reset));  // open: Qn, preset, en
  D_Flip_Flop #(.trigger("falling")) Wait_PC_load_3 (
    .clk(clk), .D(or_6_out), .Q(M_I__valid), .reset(Reset));  // open: Qn, preset, en
  or or_6 (or_6_out, demultiplexer_1_out0, CS5, pop_lw_ready, tty_enable, kbd_enable);
  D_Flip_Flop #(.trigger("falling")) END (.clk(clk), .D(M_I__valid), .Q(END_q), .reset(Reset));  // open: Qn, preset, en
  or or_7 (CS, CS1, CS2, CS3, M_I__valid, Inst_ready, CS5, pop_lw_ready);
  or or_8 (Load_Registers, M_I__valid, pop_lw_ready, CS5);
  or or_9 (Deactivate_nR_W, CS1, Inst_ready, Deactivate_nR_W_2);

  assign PC_load = M_I__valid;

  // Other names for the same wires on the sheet: CS4 = Inst_ready; Deactivate_nR_W_1 = Inst_ready;
  //   Deactivate_nR_W_t = CS1; CS7 = M_I__valid; Load_Registers_1 = M_I__valid; Load_Registers_3 = CS5;
  //   CS6 = pop_lw_ready; Load_Registers_2 = pop_lw_ready; pop__lw_ready = pop_lw_ready

  // Notes on the sheet:
  //   default
  //   pop/lw
  //   push
  //   tty
  //   halt
  //   kbd
endmodule

module Wait_WT (
  input  in_1,
  input  [3:0] WT,
  input  start,
  output CS,
  output ready,
  output Invalidate_cache_address
);

  wire and_1_out, comparator_1_eq, or_1_out, or_2_out;
  wire [3:0] counter_1_q;

  and and_1 (and_1_out, ~comparator_1_eq, CS);  // AND_Gate
  or or_1 (or_1_out, and_1_out, start);
  D_Flip_Flop #(.trigger("falling")) Read_Inst (.clk(in_1), .D(or_1_out), .Q(CS));  // open: Qn, preset, en, reset
  Counter #(.width(4), .max('hf)) counter_1 (
    .count(CS), .Q(counter_1_q), .clk(in_1), .clr(or_2_out));  // open: load, D, carry
  or or_2 (or_2_out, ready, start);
  Comparator #(.width(4)) comparator_1 (.a(WT), .b(counter_1_q), .eq(comparator_1_eq));  // open: gt, lt
  D_Flip_Flop #(.trigger("falling")) d_ff_1 (
    .clk(in_1), .D(comparator_1_eq), .Q(ready));  // open: Qn, preset, en, reset

  assign Invalidate_cache_address = CS;

  // Other names for the same wires on the sheet: clk = in_1
endmodule

// L-E
module Little_Endian_adjuster (
  input  [31:0] Input,
  output [31:0] Output
);


  assign Output = {Input[7:0], Input[15:8], Input[23:16], Input[31:24]};
endmodule
module Cache (
  input  Invalidate_cache_address,
  input  pop_lw_ready,
  input  clk,
  input  Inst_ready,
  input  [15:0] Address,
  input  CS,
  input  nR_W,
  input  reset,
  input  [31:0] RAM_Out_0,
  input  [31:0] RAM_Out_1,
  input  [31:0] RAM_Out_2,
  input  [31:0] RAM_Out_3,
  output Output,
  output Output_2,
  output Output_3,
  output Output_4,
  output Output_5,
  output Output_6,
  output Output_7,
  output Output_8,
  output Contains_current_address,
  output [31:0] RAM_Out_0_2,
  output Output_9,
  output [31:0] RAM_Out_1_2,
  output [31:0] RAM_Out_2_2,
  output [31:0] RAM_Out_3_2
);

  wire Enable, Enable_R23, Enable_row_0, Enable_row_1, Enable_row_2, Enable_row_3, Enable_row_4,
       Enable_row_5, Enable_row_6, Enable_row_7, Enable_row_8, Enable_row_9, Enable_row_10, Enable_row_11,
       Enable_row_12, Enable_row_13, Enable_row_14, Enable_row_15, Invalidate_0, Invalidate_1, Invalidate_2,
       Invalidate_3, Invalidate_4, Invalidate_5, Invalidate_6, Invalidate_7, Invalidate_8, Invalidate_9,
       Invalidate_10, Invalidate_11, Invalidate_12, Invalidate_13, Invalidate_14, Invalidate_15, or_1_out,
       or_2_out, or_3_out, or_4_out, or_5_out, or_6_out, or_7_out, or_8_out, or_9_out, or_10_out, or_11_out,
       or_12_out, or_13_out, or_14_out, or_15_out, or_16_out, or_17_out, or_18_out, Valid_0, Valid_1,
       Valid_2, Valid_3, Valid_4, Valid_5, Valid_6, Valid_7, Valid_8, Valid_9, Valid_10, Valid_11, Valid_12,
       Valid_13, Valid_14, Valid_15, Valid_Data_in_index, Valid_Tag;
  wire [11:0] Cache_tag, Tag_0, Tag_1, Tag_2, Tag_3, Tag_4, Tag_5, Tag_6, Tag_7, Tag_8, Tag_9, Tag_10,
       Tag_11, Tag_12, Tag_13, Tag_14, Tag_15;
  wire [31:0] _0_1, _0_2, _0_3, _0_4, _0_5, _0_6, _0_7, _0_8, _0_9, _0_10, _0_11, _0_12, _0_13, _0_14, _0_15,
       _0_16, _1_1, _1_2, _1_3, _1_4, _1_5, _1_6, _1_7, _1_8, _1_9, _1_10, _1_11, _1_12, _1_13, _1_14, _1_15,
       _1_16, _2_1, _2_2, _2_3, _2_4, _2_5, _2_6, _2_7, _2_8, _2_9, _2_10, _2_11, _2_12, _2_13, _2_14, _2_15,
       _2_16, _3_1, _3_2, _3_3, _3_4, _3_5, _3_6, _3_7, _3_8, _3_9, _3_10, _3_11, _3_12, _3_13, _3_14, _3_15,
       _3_16, multiplexer_3_out, multiplexer_4_out, multiplexer_5_out, multiplexer_6_out, RAM_Out_0_t,
       RAM_Out_1_t, RAM_Out_2_t, RAM_Out_3_t;

  Comparator #(.width(12)) comparator_1 (.a(Cache_tag), .b(Address[15:4]), .eq(Valid_Tag));  // open: gt, lt
  Little_Endian_adjuster little_endian_adjuster_1 (.Input(RAM_Out_0), .Output(RAM_Out_0_t));
  Little_Endian_adjuster little_endian_adjuster_2 (.Input(RAM_Out_1), .Output(RAM_Out_1_t));
  Little_Endian_adjuster little_endian_adjuster_3 (.Input(RAM_Out_2), .Output(RAM_Out_2_t));
  Little_Endian_adjuster little_endian_adjuster_4 (.Input(RAM_Out_3), .Output(RAM_Out_3_t));
  Multiplexer #(.select(4)) multiplexer_1 (
    .in0(Valid_0), .in1(Valid_1), .in2(Valid_2), .in3(Valid_3), .in4(Valid_4), .in5(Valid_5), .in6(Valid_6),
    .in7(Valid_7), .in8(Valid_8), .in9(Valid_9), .in10(Valid_10), .in11(Valid_11), .in12(Valid_12),
    .in13(Valid_13), .in14(Valid_14), .in15(Valid_15), .out(Valid_Data_in_index), .sel(Address[3:0]));  // open: en
  or or_1 (or_1_out, Inst_ready, pop_lw_ready);
  and and_1 (Contains_current_address, Valid_Data_in_index, Valid_Tag);
  and and_2 (Enable, ~nR_W, or_1_out, CS);  // AND_Gate
  Demultiplexer #(.select(4)) demultiplexer_1 (
    .out0(Enable_row_0), .out1(Enable_row_1), .out2(Enable_row_2), .out3(Enable_row_3), .out4(Enable_row_4),
    .out5(Enable_row_5), .out6(Enable_row_6), .out7(Enable_row_7), .out8(Enable_row_8), .out9(Enable_row_9),
    .out10(Enable_row_10), .out11(Enable_row_11), .out12(Enable_row_12), .out13(Enable_row_13),
    .out14(Enable_row_14), .out15(Enable_row_15), .in(Enable), .sel(Address[3:0]));  // open: en
  or or_2 (or_2_out, Invalidate_cache_address, reset);
  Demultiplexer #(.select(4)) demultiplexer_2 (
    .out0(Invalidate_0), .out1(Invalidate_1), .out2(Invalidate_2), .out3(Invalidate_3), .out4(Invalidate_4),
    .out5(Invalidate_5), .out6(Invalidate_6), .out7(Invalidate_7), .out8(Invalidate_8), .out9(Invalidate_9),
    .out10(Invalidate_10), .out11(Invalidate_11), .out12(Invalidate_12), .out13(Invalidate_13),
    .out14(Invalidate_14), .out15(Invalidate_15), .in(or_2_out), .sel(Address[3:0]));  // open: en
  Multiplexer #(.select(4), .width(12)) multiplexer_2 (
    .in0(Tag_0), .in1(Tag_1), .in2(Tag_2), .in3(Tag_3), .in4(Tag_4), .in5(Tag_5), .in6(Tag_6), .in7(Tag_7),
    .in8(Tag_8), .in9(Tag_9), .in10(Tag_10), .in11(Tag_11), .in12(Tag_12), .in13(Tag_13), .in14(Tag_14),
    .in15(Tag_15), .out(Cache_tag), .sel(Address[3:0]));  // open: en
  Register #(.width(12)) R0 (.D(Address[15:4]), .en(Enable_row_0), .Q(Tag_0), .clk(clk), .clr(reset));
  Register #(.width(12)) R4 (.D(Address[15:4]), .en(Enable_row_1), .Q(Tag_1), .clk(clk), .clr(reset));
  Register #(.width(12)) R8 (.D(Address[15:4]), .en(Enable_row_2), .Q(Tag_2), .clk(clk), .clr(reset));
  Register #(.width(12)) R12 (.D(Address[15:4]), .en(Enable_row_3), .Q(Tag_3), .clk(clk), .clr(reset));
  Register #(.width(12)) R16 (.D(Address[15:4]), .en(Enable_row_4), .Q(Tag_4), .clk(clk), .clr(reset));
  Register #(.width(12)) R20 (.D(Address[15:4]), .en(Enable_row_5), .Q(Tag_5), .clk(clk), .clr(reset));
  Register #(.width(12)) R24 (.D(Address[15:4]), .en(Enable_row_6), .Q(Tag_6), .clk(clk), .clr(reset));
  Register #(.width(12)) R28 (.D(Address[15:4]), .en(Enable_row_7), .Q(Tag_7), .clk(clk), .clr(reset));
  Register #(.width(12)) R0_2 (.D(Address[15:4]), .en(Enable_row_8), .Q(Tag_8), .clk(clk), .clr(reset));
  Register #(.width(12)) R4_2 (.D(Address[15:4]), .en(Enable_row_9), .Q(Tag_9), .clk(clk), .clr(reset));
  Register #(.width(12)) R8_2 (.D(Address[15:4]), .en(Enable_row_10), .Q(Tag_10), .clk(clk), .clr(reset));
  Register #(.width(12)) R12_2 (.D(Address[15:4]), .en(Enable_row_11), .Q(Tag_11), .clk(clk), .clr(reset));
  Register #(.width(12)) R16_2 (.D(Address[15:4]), .en(Enable_row_12), .Q(Tag_12), .clk(clk), .clr(reset));
  Register #(.width(12)) R20_2 (.D(Address[15:4]), .en(Enable_row_13), .Q(Tag_13), .clk(clk), .clr(reset));
  Register #(.width(12)) R24_2 (.D(Address[15:4]), .en(Enable_row_14), .Q(Tag_14), .clk(clk), .clr(reset));
  Register #(.width(12)) R28_2 (.D(Address[15:4]), .en(Enable_row_15), .Q(Tag_15), .clk(clk), .clr(reset));
  Register #(.width(32)) R0_3 (.D(RAM_Out_0_t), .en(Enable_row_0), .Q(_0_1), .clk(clk), .clr(reset));
  Register #(.width(32)) R4_3 (.D(RAM_Out_0_t), .en(Enable_row_1), .Q(_0_2), .clk(clk), .clr(reset));
  Register #(.width(32)) R8_3 (.D(RAM_Out_0_t), .en(Enable_row_2), .Q(_0_3), .clk(clk), .clr(reset));
  Register #(.width(32)) R12_3 (.D(RAM_Out_0_t), .en(Enable_row_3), .Q(_0_4), .clk(clk), .clr(reset));
  Register #(.width(32)) R16_3 (.D(RAM_Out_0_t), .en(Enable_row_4), .Q(_0_5), .clk(clk), .clr(reset));
  Register #(.width(32)) R20_3 (.D(RAM_Out_0_t), .en(Enable_row_5), .Q(_0_6), .clk(clk), .clr(reset));
  Register #(.width(32)) R24_3 (.D(RAM_Out_0_t), .en(Enable_row_6), .Q(_0_7), .clk(clk), .clr(reset));
  Register #(.width(32)) R28_3 (.D(RAM_Out_0_t), .en(Enable_row_7), .Q(_0_8), .clk(clk), .clr(reset));
  Register #(.width(32)) R0_4 (.D(RAM_Out_0_t), .en(Enable_row_8), .Q(_0_9), .clk(clk), .clr(reset));
  Register #(.width(32)) R4_4 (.D(RAM_Out_0_t), .en(Enable_row_9), .Q(_0_10), .clk(clk), .clr(reset));
  Register #(.width(32)) R8_4 (.D(RAM_Out_0_t), .en(Enable_row_10), .Q(_0_11), .clk(clk), .clr(reset));
  Register #(.width(32)) R12_4 (.D(RAM_Out_0_t), .en(Enable_row_11), .Q(_0_12), .clk(clk), .clr(reset));
  Register #(.width(32)) R16_4 (.D(RAM_Out_0_t), .en(Enable_row_12), .Q(_0_13), .clk(clk), .clr(reset));
  Register #(.width(32)) R20_4 (.D(RAM_Out_0_t), .en(Enable_row_13), .Q(_0_14), .clk(clk), .clr(reset));
  Register #(.width(32)) R24_4 (.D(RAM_Out_0_t), .en(Enable_row_14), .Q(_0_15), .clk(clk), .clr(reset));
  Register #(.width(32)) R28_4 (.D(RAM_Out_0_t), .en(Enable_row_15), .Q(_0_16), .clk(clk), .clr(reset));
  Register #(.width(32)) R1 (.D(RAM_Out_1_t), .en(Enable_row_0), .Q(_1_1), .clk(clk), .clr(reset));
  Register #(.width(32)) R5 (.D(RAM_Out_1_t), .en(Enable_row_1), .Q(_1_2), .clk(clk), .clr(reset));
  Register #(.width(32)) R9 (.D(RAM_Out_1_t), .en(Enable_row_2), .Q(_1_3), .clk(clk), .clr(reset));
  Register #(.width(32)) R13 (.D(RAM_Out_1_t), .en(Enable_row_3), .Q(_1_4), .clk(clk), .clr(reset));
  Register #(.width(32)) R17 (.D(RAM_Out_1_t), .en(Enable_row_4), .Q(_1_5), .clk(clk), .clr(reset));
  Register #(.width(32)) R21 (.D(RAM_Out_1_t), .en(Enable_row_5), .Q(_1_6), .clk(clk), .clr(reset));
  Register #(.width(32)) R25 (.D(RAM_Out_1_t), .en(Enable_row_6), .Q(_1_7), .clk(clk), .clr(reset));
  Register #(.width(32)) R29 (.D(RAM_Out_1_t), .en(Enable_row_7), .Q(_1_8), .clk(clk), .clr(reset));
  Register #(.width(32)) R1_2 (.D(RAM_Out_1_t), .en(Enable_row_8), .Q(_1_9), .clk(clk), .clr(reset));
  Register #(.width(32)) R5_2 (.D(RAM_Out_1_t), .en(Enable_row_9), .Q(_1_10), .clk(clk), .clr(reset));
  Register #(.width(32)) R9_2 (.D(RAM_Out_1_t), .en(Enable_row_10), .Q(_1_11), .clk(clk), .clr(reset));
  Register #(.width(32)) R13_2 (.D(RAM_Out_1_t), .en(Enable_row_11), .Q(_1_12), .clk(clk), .clr(reset));
  Register #(.width(32)) R17_2 (.D(RAM_Out_1_t), .en(Enable_row_12), .Q(_1_13), .clk(clk), .clr(reset));
  Register #(.width(32)) R21_2 (.D(RAM_Out_1_t), .en(Enable_row_13), .Q(_1_14), .clk(clk), .clr(reset));
  Register #(.width(32)) R25_2 (.D(RAM_Out_1_t), .en(Enable_row_14), .Q(_1_15), .clk(clk), .clr(reset));
  Register #(.width(32)) R29_2 (.D(RAM_Out_1_t), .en(Enable_row_15), .Q(_1_16), .clk(clk), .clr(reset));
  Register #(.width(32)) R2 (.D(RAM_Out_2_t), .en(Enable_row_0), .Q(_2_1), .clk(clk), .clr(reset));
  Register #(.width(32)) R6 (.D(RAM_Out_2_t), .en(Enable_row_1), .Q(_2_2), .clk(clk), .clr(reset));
  Register #(.width(32)) R10 (.D(RAM_Out_2_t), .en(Enable_row_2), .Q(_2_3), .clk(clk), .clr(reset));
  Register #(.width(32)) R14 (.D(RAM_Out_2_t), .en(Enable_row_3), .Q(_2_4), .clk(clk), .clr(reset));
  Register #(.width(32)) R18 (.D(RAM_Out_2_t), .en(Enable_row_4), .Q(_2_5), .clk(clk), .clr(reset));
  Register #(.width(32)) R22 (.D(RAM_Out_2_t), .en(Enable_row_5), .Q(_2_6), .clk(clk), .clr(reset));
  Register #(.width(32)) R26 (.D(RAM_Out_2_t), .en(Enable_row_6), .Q(_2_7), .clk(clk), .clr(reset));
  Register #(.width(32)) R30 (.D(RAM_Out_2_t), .en(Enable_row_7), .Q(_2_8), .clk(clk), .clr(reset));
  Register #(.width(32)) R2_2 (.D(RAM_Out_2_t), .en(Enable_row_8), .Q(_2_9), .clk(clk), .clr(reset));
  Register #(.width(32)) R6_2 (.D(RAM_Out_2_t), .en(Enable_row_9), .Q(_2_10), .clk(clk), .clr(reset));
  Register #(.width(32)) R10_2 (.D(RAM_Out_2_t), .en(Enable_row_10), .Q(_2_11), .clk(clk), .clr(reset));
  Register #(.width(32)) R14_2 (.D(RAM_Out_2_t), .en(Enable_row_11), .Q(_2_12), .clk(clk), .clr(reset));
  Register #(.width(32)) R18_2 (.D(RAM_Out_2_t), .en(Enable_row_12), .Q(_2_13), .clk(clk), .clr(reset));
  Register #(.width(32)) R22_2 (.D(RAM_Out_2_t), .en(Enable_row_13), .Q(_2_14), .clk(clk), .clr(reset));
  Register #(.width(32)) R26_2 (.D(RAM_Out_2_t), .en(Enable_row_14), .Q(_2_15), .clk(clk), .clr(reset));
  Register #(.width(32)) R30_2 (.D(RAM_Out_2_t), .en(Enable_row_15), .Q(_2_16), .clk(clk), .clr(reset));
  Register #(.width(32)) R3 (.D(RAM_Out_3_t), .en(Enable_row_0), .Q(_3_1), .clk(clk), .clr(reset));
  Register #(.width(32)) R7 (.D(RAM_Out_3_t), .en(Enable_row_1), .Q(_3_2), .clk(clk), .clr(reset));
  Register #(.width(32)) R11 (.D(RAM_Out_3_t), .en(Enable_row_2), .Q(_3_3), .clk(clk), .clr(reset));
  Register #(.width(32)) R15 (.D(RAM_Out_3_t), .en(Enable_row_3), .Q(_3_4), .clk(clk), .clr(reset));
  Register #(.width(32)) R19 (.D(RAM_Out_3_t), .en(Enable_row_4), .Q(_3_5), .clk(clk), .clr(reset));
  Register #(.width(32)) R23 (.D(RAM_Out_3_t), .en(Enable_R23), .Q(_3_6), .clk(clk), .clr(reset));
  Register #(.width(32)) R27 (.D(RAM_Out_3_t), .en(Enable_row_6), .Q(_3_7), .clk(clk), .clr(reset));
  Register #(.width(32)) R31 (.D(RAM_Out_3_t), .en(Enable_row_7), .Q(_3_8), .clk(clk), .clr(reset));
  Register #(.width(32)) R3_2 (.D(RAM_Out_3_t), .en(Enable_row_8), .Q(_3_9), .clk(clk), .clr(reset));
  Register #(.width(32)) R7_2 (.D(RAM_Out_3_t), .en(Enable_row_9), .Q(_3_10), .clk(clk), .clr(reset));
  Register #(.width(32)) R11_2 (.D(RAM_Out_3_t), .en(Enable_row_10), .Q(_3_11), .clk(clk), .clr(reset));
  Register #(.width(32)) R15_2 (.D(RAM_Out_3_t), .en(Enable_row_11), .Q(_3_12), .clk(clk), .clr(reset));
  Register #(.width(32)) R19_2 (.D(RAM_Out_3_t), .en(Enable_row_12), .Q(_3_13), .clk(clk), .clr(reset));
  Register #(.width(32)) R23_2 (.D(RAM_Out_3_t), .en(Enable_row_13), .Q(_3_14), .clk(clk), .clr(reset));
  Register #(.width(32)) R27_2 (.D(RAM_Out_3_t), .en(Enable_row_14), .Q(_3_15), .clk(clk), .clr(reset));
  Register #(.width(32)) R31_2 (.D(RAM_Out_3_t), .en(Enable_row_15), .Q(_3_16), .clk(clk), .clr(reset));
  D_Flip_Flop #(.trigger("falling")) d_ff_1 (
    .clk(clk), .D(or_3_out), .Q(Valid_0), .reset(Invalidate_0));  // open: Qn, preset, en
  or or_3 (or_3_out, Valid_0, Enable_row_0);
  D_Flip_Flop #(.trigger("falling")) d_ff_2 (
    .clk(clk), .D(or_4_out), .Q(Valid_1), .reset(Invalidate_1));  // open: Qn, preset, en
  or or_4 (or_4_out, Valid_1, Enable_row_1);
  D_Flip_Flop #(.trigger("falling")) d_ff_3 (
    .clk(clk), .D(or_5_out), .Q(Valid_2), .reset(Invalidate_2));  // open: Qn, preset, en
  or or_5 (or_5_out, Valid_2, Enable_row_2);
  D_Flip_Flop #(.trigger("falling")) d_ff_4 (
    .clk(clk), .D(or_6_out), .Q(Valid_3), .reset(Invalidate_3));  // open: Qn, preset, en
  or or_6 (or_6_out, Valid_3, Enable_row_3);
  D_Flip_Flop #(.trigger("falling")) d_ff_5 (
    .clk(clk), .D(or_7_out), .Q(Valid_4), .reset(Invalidate_4));  // open: Qn, preset, en
  or or_7 (or_7_out, Valid_4, Enable_row_4);
  D_Flip_Flop #(.trigger("falling")) d_ff_6 (
    .clk(clk), .D(or_8_out), .Q(Valid_5), .reset(Invalidate_5));  // open: Qn, preset, en
  or or_8 (or_8_out, Valid_5, Enable_row_5);
  D_Flip_Flop #(.trigger("falling")) d_ff_7 (
    .clk(clk), .D(or_9_out), .Q(Valid_6), .reset(Invalidate_6));  // open: Qn, preset, en
  or or_9 (or_9_out, Valid_6, Enable_row_6);
  D_Flip_Flop #(.trigger("falling")) d_ff_8 (
    .clk(clk), .D(or_10_out), .Q(Valid_7), .reset(Invalidate_7));  // open: Qn, preset, en
  or or_10 (or_10_out, Valid_7, Enable_row_7);
  D_Flip_Flop #(.trigger("falling")) d_ff_9 (
    .clk(clk), .D(or_11_out), .Q(Valid_8), .reset(Invalidate_8));  // open: Qn, preset, en
  or or_11 (or_11_out, Valid_8, Enable_row_8);
  D_Flip_Flop #(.trigger("falling")) d_ff_10 (
    .clk(clk), .D(or_12_out), .Q(Valid_9), .reset(Invalidate_9));  // open: Qn, preset, en
  or or_12 (or_12_out, Valid_9, Enable_row_9);
  D_Flip_Flop #(.trigger("falling")) d_ff_11 (
    .clk(clk), .D(or_13_out), .Q(Valid_10), .reset(Invalidate_10));  // open: Qn, preset, en
  or or_13 (or_13_out, Valid_10, Enable_row_10);
  D_Flip_Flop #(.trigger("falling")) d_ff_12 (
    .clk(clk), .D(or_14_out), .Q(Valid_11), .reset(Invalidate_11));  // open: Qn, preset, en
  or or_14 (or_14_out, Valid_11, Enable_row_11);
  D_Flip_Flop #(.trigger("falling")) d_ff_13 (
    .clk(clk), .D(or_15_out), .Q(Valid_12), .reset(Invalidate_12));  // open: Qn, preset, en
  or or_15 (or_15_out, Valid_12, Enable_row_12);
  D_Flip_Flop #(.trigger("falling")) d_ff_14 (
    .clk(clk), .D(or_16_out), .Q(Valid_13), .reset(Invalidate_13));  // open: Qn, preset, en
  or or_16 (or_16_out, Valid_13, Enable_row_13);
  D_Flip_Flop #(.trigger("falling")) d_ff_15 (
    .clk(clk), .D(or_17_out), .Q(Valid_14), .reset(Invalidate_14));  // open: Qn, preset, en
  or or_17 (or_17_out, Valid_14, Enable_row_14);
  D_Flip_Flop #(.trigger("falling")) d_ff_16 (
    .clk(clk), .D(or_18_out), .Q(Valid_15), .reset(Invalidate_15));  // open: Qn, preset, en
  or or_18 (or_18_out, Valid_15, Enable_row_15);
  Little_Endian_adjuster little_endian_adjuster_5 (.Input(multiplexer_3_out), .Output(RAM_Out_0_2));
  Multiplexer #(.select(4), .width(32)) multiplexer_3 (
    .in0(_0_1), .in1(_0_2), .in2(_0_3), .in3(_0_4), .in4(_0_5), .in5(_0_6), .in6(_0_7), .in7(_0_8),
    .in8(_0_9), .in9(_0_10), .in10(_0_11), .in11(_0_12), .in12(_0_13), .in13(_0_14), .in14(_0_15),
    .in15(_0_16), .out(multiplexer_3_out), .sel(Address[3:0]));  // open: en
  Little_Endian_adjuster little_endian_adjuster_6 (.Input(multiplexer_4_out), .Output(RAM_Out_1_2));
  Multiplexer #(.select(4), .width(32)) multiplexer_4 (
    .in0(_1_1), .in1(_1_2), .in2(_1_3), .in3(_1_4), .in4(_1_5), .in5(_1_6), .in6(_1_7), .in7(_1_8),
    .in8(_1_9), .in9(_1_10), .in10(_1_11), .in11(_1_12), .in12(_1_13), .in13(_1_14), .in14(_1_15),
    .in15(_1_16), .out(multiplexer_4_out), .sel(Address[3:0]));  // open: en
  Multiplexer #(.select(4), .width(32)) multiplexer_5 (
    .in0(_2_1), .in1(_2_2), .in2(_2_3), .in3(_2_4), .in4(_2_5), .in5(_2_6), .in6(_2_7), .in7(_2_8),
    .in8(_2_9), .in9(_2_10), .in10(_2_11), .in11(_2_12), .in12(_2_13), .in13(_2_14), .in14(_2_15),
    .in15(_2_16), .out(multiplexer_5_out), .sel(Address[3:0]));  // open: en
  Little_Endian_adjuster little_endian_adjuster_7 (.Input(multiplexer_5_out), .Output(RAM_Out_2_2));
  Little_Endian_adjuster little_endian_adjuster_8 (.Input(multiplexer_6_out), .Output(RAM_Out_3_2));
  Multiplexer #(.select(4), .width(32)) multiplexer_6 (
    .in0(_3_1), .in1(_3_2), .in2(_3_3), .in3(_3_4), .in4(_3_5), .in5(_3_6), .in6(_3_7), .in7(_3_8),
    .in8(_3_9), .in9(_3_10), .in10(_3_11), .in11(_3_12), .in12(_3_13), .in13(_3_14), .in14(_3_15),
    .in15(_3_16), .out(multiplexer_6_out), .sel(Address[3:0]));  // open: en

  assign Output = 1'b1;
  assign Output_2 = 1'b1;
  assign Output_3 = 1'b1;
  assign Output_4 = 1'b1;
  assign Output_5 = 1'b1;
  assign Output_6 = 1'b1;
  assign Output_7 = 1'b1;
  assign Output_8 = 1'b1;

  // Other names for the same wires on the sheet: index[3:0] = Address[3:0]; Tag[11:0] = Address[15:4]

  // Notes on the sheet:
  //   Tag
  //   Index
  //   Offset
  //   Valid
endmodule

module Wait_RT (
  input  clk,
  input  [3:0] RT,
  input  Cached,
  input  start,
  output CS,
  output ready
);

  wire and_1_out, and_2_out, comparator_1_eq, demultiplexer_1_out1, or_1_out, or_2_out, or_3_out, Read_Inst_q;
  wire [3:0] counter_1_q;

  and and_1 (and_1_out, ~comparator_1_eq, Read_Inst_q);  // AND_Gate
  or or_1 (or_1_out, and_1_out, start);
  D_Flip_Flop #(.trigger("falling")) Read_Inst (
    .clk(clk), .D(or_1_out), .Q(Read_Inst_q));  // open: Qn, preset, en, reset
  Demultiplexer demultiplexer_1 (
    .out0(CS), .out1(demultiplexer_1_out1), .in(Read_Inst_q), .sel(and_2_out));  // open: en
  and and_2 (and_2_out, Read_Inst_q, Cached);
  Counter #(.width(4), .max('hf)) counter_1 (
    .count(CS), .Q(counter_1_q), .clk(clk), .clr(or_2_out));  // open: load, D, carry
  or or_2 (or_2_out, ready, start);
  Comparator #(.width(4)) comparator_1 (.a(RT), .b(counter_1_q), .eq(comparator_1_eq));  // open: gt, lt
  or or_3 (or_3_out, demultiplexer_1_out1, comparator_1_eq);
  D_Flip_Flop #(.trigger("falling")) d_ff_1 (.clk(clk), .D(or_3_out), .Q(ready));  // open: Qn, preset, en, reset
endmodule
